# Fritzing sketch 10mm LED Light Board (saved by Fritzing 0.6.4b)
breadboards: 1

parts:
  LED1 = LED - 5mm [color="Red (633nm)" package="5 mm [THT]"]
  J1 = female pin header, 2 pins [form="♀ (female)"]
  LED2 = LED - 5mm [color="Red (633nm)" package="5 mm [THT]"]
  LED3 = LED - 5mm [color="Red (633nm)" package="5 mm [THT]"]
  LED4 = LED - 5mm [color="Red (633nm)" package="5 mm [THT]"]
  LED5 = LED - 5mm [color="Red (633nm)" package="5 mm [THT]"]
  LED6 = LED - 5mm [color="Red (633nm)" package="5 mm [THT]"]
  LED7 = LED - 5mm [color="Red (633nm)" package="5 mm [THT]"]
  LED8 = LED - 5mm [color="Red (633nm)" package="5 mm [THT]"]
  LED9 = LED - 5mm [color="Red (633nm)" package="5 mm [THT]"]
  LED10 = LED - 5mm [color="Red (633nm)" package="5 mm [THT]"]
  LED11 = LED - 5mm [color="Red (633nm)" package="5 mm [THT]"]
  LED12 = LED - 5mm [color="Red (633nm)" package="5 mm [THT]"]
  R1 = Resistor [tolerance=±5% resistance=220 package=THT]
  R2 = Resistor [tolerance=±5% resistance=220 package=THT]
  R3 = Resistor [tolerance=±5% resistance=220 package=THT]
  R4 = Resistor [tolerance=±5% resistance=220 package=THT]
  J2 = female pin header, 2 pins [form="♀ (female)"]

nets:
  N1: LED1.cathode, J1.pin1, LED4.cathode, LED7.cathode, LED10.cathode, J2.pin1
  N2: LED1.anode, LED2.cathode
  N3: J1.pin2, R1.Pin_0, R2.Pin_0, R3.Pin_0, R4.Pin_0, J2.pin2
  N4: LED2.anode, LED3.cathode
  N5: LED3.anode, R1.Pin_1
  N6: LED4.anode, LED5.cathode
  N7: LED5.anode, LED6.cathode
  N8: LED6.anode, R2.Pin_1
  N9: LED7.anode, LED8.cathode
  N10: LED8.anode, LED9.cathode
  N11: LED9.anode, R3.Pin_1
  N12: LED10.anode, LED11.cathode
  N13: LED11.anode, LED12.cathode
  N14: LED12.anode, R4.Pin_1
