# Fritzing sketch 10mm LED Tail Light Board (saved by Fritzing 0.7.1b)
breadboards: 1

parts:
  LED1 = LED - 5mm [color="Red (633nm)" package="5 mm [THT]"]
  LED2 = LED - 5mm [color="Red (633nm)" package="5 mm [THT]"]
  LED3 = LED - 5mm [color="Red (633nm)" package="5 mm [THT]"]
  LED4 = LED - 5mm [color="Red (633nm)" package="5 mm [THT]"]
  LED5 = LED - 5mm [color="Red (633nm)" package="5 mm [THT]"]
  LED6 = LED - 5mm [color="Red (633nm)" package="5 mm [THT]"]
  LED7 = LED - 5mm [color="Red (633nm)" package="5 mm [THT]"]
  LED8 = LED - 5mm [color="Red (633nm)" package="5 mm [THT]"]
  LED9 = LED - 5mm [color="Red (633nm)" package="5 mm [THT]"]
  LED10 = LED - 5mm [color="Red (633nm)" package="5 mm [THT]"]
  LED11 = LED - 5mm [color="Red (633nm)" package="5 mm [THT]"]
  LED12 = LED - 5mm [color="Red (633nm)" package="5 mm [THT]"]
  R1 = Resistor [tolerance=±5% resistance=220 package=THT]
  R2 = Resistor [tolerance=±5% resistance=220 package=THT]
  R3 = Resistor [tolerance=±5% resistance=220 package=THT]
  R4 = Resistor [tolerance=±5% resistance=220 package=THT]
  J2 = female pin header, 3 pins [form="♀ (female)"]
  R5 = Resistor [tolerance=±5% resistance=220 package=THT]
  LED13 = LED - 5mm [color="Red (633nm)" package="5 mm [THT]"]
  LED14 = LED - 5mm [color="Red (633nm)" package="5 mm [THT]"]
  LED15 = LED - 5mm [color="Red (633nm)" package="5 mm [THT]"]
  LED16 = LED - 5mm [color="Red (633nm)" package="5 mm [THT]"]
  LED17 = LED - 5mm [color="Red (633nm)" package="5 mm [THT]"]
  LED18 = LED - 5mm [color="Red (633nm)" package="5 mm [THT]"]
  R6 = Resistor [tolerance=±5% resistance=220 package=THT]
  D2 = Rectifier Diode [part_number=1N4001 package="300 mil [THT]"]
  D3 = Rectifier Diode [part_number=1N4001 package="300 mil [THT]"]

nets:
  N1: LED1.cathode, LED4.cathode, LED7.cathode
  N2: LED1.anode, LED2.cathode
  N3: LED2.anode, LED3.cathode
  N4: LED3.anode, R1.Pin_1
  N5: LED4.anode, LED5.cathode
  N6: LED5.anode, LED6.cathode
  N7: LED6.anode, R2.Pin_1
  N8: LED7.anode, LED8.cathode
  N9: LED8.anode, LED9.cathode
  N10: LED9.anode, R4.Pin_1
  N11: LED10.cathode, D2.cathode, D3.cathode
  N12: LED10.anode, LED11.cathode
  N13: LED11.anode, LED12.cathode
  N14: LED12.anode, R3.Pin_1
  N15: R1.Pin_0, R2.Pin_0, R3.Pin_0, R4.Pin_0, J2.pin3, R5.Pin_1, R6.Pin_1
  N16: J2.pin1, D3.anode
  N17: J2.pin2, LED15.anode, LED18.anode, D2.anode
  N18: R5.Pin_0, LED13.cathode
  N19: LED13.anode, LED14.cathode
  N20: LED14.anode, LED15.cathode
  N21: LED16.cathode, R6.Pin_0
  N22: LED16.anode, LED17.cathode
  N23: LED17.anode, LED18.cathode
