# Fritzing sketch 16ch PWM Board (saved by Fritzing 0.7.0b)
breadboards: 1

parts:
  IC1 = ULN2803A [package=THT]
  IC2 = ULN2803A [package=THT]
  J1 = female pin header, 16 pins [form="♀ (female)"]
  IC3 = IC, DIP package, 28 pins [chip_label=IC spacing=300mil]
  IC4 = IC, DIP package, 20 pins [chip_label=IC spacing=300mil]
  IC5 = IC, DIP package, 20 pins [chip_label=IC spacing=300mil]
  J2 = female pin header, 7 pins [form="♀ (female)"]
  R1 = Resistor [tolerance=±5% resistance=220 package=THT]
  R2 = Resistor [tolerance=±5% resistance=220 package=THT]
  LED1 = LED - 3mm [color="Red (633nm)" package="3 mm [THT]"]
  R3 = Resistor [tolerance=±5% resistance=220 package=THT]

nets:
  N1: IC1.In_1, IC4.pin18
  N2: IC1.In_2, IC4.pin17
  N3: IC1.In_3, IC4.pin16
  N4: IC1.In_4, IC4.pin15
  N5: IC1.In_5, IC4.pin14
  N6: IC1.In_6, IC4.pin13
  N7: IC1.In_7, IC4.pin12
  N8: IC1.In_8, IC4.pin11
  N9: IC1.0V, IC1.COM_-_Common, IC2.0V, IC2.COM_-_Common, IC3.pin8, IC3.pin13, IC4.pin10, IC5.pin10, J2.pin2, R2.Pin_0, R3.Pin_0
  N10: IC1.Out_8, J1.pin8
  N11: IC1.Out_7, J1.pin7
  N12: IC1.Out_6, J1.pin6
  N13: IC1.Out_5, J1.pin5
  N14: IC1.Out_4, J1.pin4
  N15: IC1.Out_3, J1.pin3
  N16: IC1.Out_2, J1.pin2
  N17: IC1.Out_1, J1.pin1
  N18: IC2.In_1, IC5.pin18
  N19: IC2.In_2, IC5.pin17
  N20: IC2.In_3, IC5.pin16
  N21: IC2.In_4, IC5.pin15
  N22: IC2.In_5, IC5.pin14
  N23: IC2.In_6, IC5.pin13
  N24: IC2.In_7, IC5.pin12
  N25: IC2.In_8, IC5.pin11
  N26: IC2.Out_8, J1.pin16
  N27: IC2.Out_7, J1.pin15
  N28: IC2.Out_6, J1.pin14
  N29: IC2.Out_5, J1.pin13
  N30: IC2.Out_4, J1.pin12
  N31: IC2.Out_3, J1.pin11
  N32: IC2.Out_2, J1.pin10
  N33: IC2.Out_1, J1.pin9
  N34: IC3.pin1, IC4.pin2
  N35: IC3.pin4, J2.pin3
  N36: IC3.pin5, IC3.pin7, IC4.pin1, IC4.pin19, IC4.pin20, IC5.pin1, IC5.pin19, IC5.pin20, J2.pin1, R1.Pin_0, LED1.anode
  N37: IC3.pin6, R2.Pin_1
  N38: IC3.pin9, J2.pin4, R1.Pin_1
  N39: IC3.pin10, J2.pin5
  N40: IC3.pin11, J2.pin6
  N41: IC3.pin12, J2.pin7
  N42: IC3.pin14, IC5.pin9
  N43: IC3.pin15, IC5.pin8
  N44: IC3.pin16, IC5.pin7
  N45: IC3.pin17, IC5.pin6
  N46: IC3.pin18, IC5.pin5
  N47: IC3.pin19, IC5.pin4
  N48: IC3.pin20, IC5.pin3
  N49: IC3.pin21, IC5.pin2
  N50: IC3.pin22, IC4.pin9
  N51: IC3.pin23, IC4.pin8
  N52: IC3.pin24, IC4.pin7
  N53: IC3.pin25, IC4.pin6
  N54: IC3.pin26, IC4.pin5
  N55: IC3.pin27, IC4.pin4
  N56: IC3.pin28, IC4.pin3
  N57: LED1.cathode, R3.Pin_1
