# Fritzing sketch ATMega - RGB Strip Connector (saved by Fritzing 0.7.0b)
breadboards: 1

parts:
  J1 = female pin header, 5 pins [form="♀ (female)"]
  J2 = female pin header, 5 pins [form="♀ (female)"]
  J3 = female pin header, 5 pins [form="♀ (female)"]
  J5 = female pin header, 5 pins [form="♀ (female)"]
  Q1 = PNP-Transistor [package="TO92 [THT]"]
  R4 = Resistor [tolerance=±5% resistance=220 package=THT]
  R5 = Resistor [tolerance=±5% resistance=220 package=THT]
  R6 = Resistor [tolerance=±5% resistance=220 package=THT]
  R7 = Resistor [tolerance=±5% resistance=220 package=THT]
  R8 = Resistor [tolerance=±5% resistance=220 package=THT]
  Q2 = PNP-Transistor [package="TO92 [THT]"]
  Q3 = PNP-Transistor [package="TO92 [THT]"]
  Q4 = PNP-Transistor [package="TO92 [THT]"]
  Q5 = PNP-Transistor [package="TO92 [THT]"]
  J7 = female pin header, 2 pins [form="♀ (female)"]
  J8 = female pin header, 5 pins [form="♀ (female)"]
  U1 = 74HC595 [package="DIP16 [THT]"]
  J9 = female pin header, 5 pins [form="♀ (female)"]

nets:
  N1: J1.pin1, J1.pin2, J1.pin3, J1.pin4, J1.pin5, U1.Q7
  N2: J2.pin1, J2.pin2, J2.pin3, J2.pin4, J2.pin5, U1.Q5
  N3: J3.pin1, J3.pin2, J3.pin3, J3.pin4, J3.pin5, U1.Q6
  N4: J5.pin1, Q3.E
  N5: J5.pin2, Q4.E
  N6: J5.pin3, Q1.E
  N7: J5.pin4, Q5.E
  N8: J5.pin5, Q2.E
  N9: Q1.B, R4.Pin_1
  N10: Q1.C, Q2.C, Q3.C, Q4.C, Q5.C, J7.pin1
  N11: R4.Pin_0, U1.Q2
  N12: R5.Pin_0, U1.Q1
  N13: R5.Pin_1, Q5.B
  N14: R6.Pin_0, U1.Q0
  N15: R6.Pin_1, Q2.B
  N16: R7.Pin_0, U1.Q3
  N17: R7.Pin_1, Q4.B
  N18: R8.Pin_0, U1.Q4
  N19: R8.Pin_1, Q3.B
  N20: J7.pin2, J8.pin1, J8.pin2, J8.pin3, J8.pin4, J8.pin5, U1.GND, U1.OE, J9.pin5
  N21: U1.MR, U1.VCC, J9.pin4
  N22: U1.SH_CP, J9.pin1
  N23: U1.ST_CP, J9.pin2
  N24: U1.DS, J9.pin3
