# Fritzing sketch ATMega8 - Stepper (saved by Fritzing 0.7.1b)
breadboards: 1

parts:
  U1 = atmega168 [package=dip]
  R1 = Resistor [tolerance=±5% resistance=220 package=THT]
  XTAL1 = Crystal [frequency="16 Mhz" package=THT]
  C2 = Ceramic Capacitor [capacitance=100nF package="100 mil [THT, multilayer]"]
  C3 = Ceramic Capacitor [capacitance=100nF package="100 mil [THT, multilayer]"]
  J1 = female pin header, 5 pins [form="♀ (female)"]

nets:
  N1: U1.RESET, R1.Pin_0
  5V: U1.VCC, U1.AVCC, U1.AREF, R1.Pin_1, J1.pin1
  GND: U1.GND, C3.0, J1.pin2
  N2: U1.XLAT1, XTAL1.pin_0, C3.1
  N3: U1.XLAT2, XTAL1.pin_1, C2.1
