# Fritzing sketch Alternating Flasher (saved by Fritzing 0.7.0b)
breadboards: 1

parts:
  R = LED - 5mm [color="Red (633nm)" package="5 mm [THT]"]
  W = LED - 5mm [color="White (6500K)" package="5 mm [THT]"]
  B = LED - 5mm [color="Blue (525nm)" package="5 mm [THT]"]
  G = LED - 5mm [color="Green (570nm)" package="5 mm [THT]"]
  U1 = 555 Timer [package="DIP8 [THT]"]
  RR = Resistor [tolerance=±5% resistance=100 package=THT]
  WR = Resistor [tolerance=±5% resistance=100 package=THT]
  BR = Resistor [tolerance=±5% resistance=100 package=THT]
  GR = Resistor [tolerance=±5% resistance=100 package=THT]
  R5 = Resistor [tolerance=±5% resistance=10k package=THT]
  C1 = Electrolytic Capacitor [capacitance=220µF package="200 mil [THT, electrolytic]"]
  VCC1 = 4 x AAA Battery Mount

nets:
  N1: R.cathode, RR.Pin_0
  N2: R.anode, W.anode, U1.Reset, U1.Vcc_Supply_Voltage, VCC1.+
  N3: W.cathode, WR.Pin_0
  N4: B.cathode, G.cathode, U1.Ground, C1.-, VCC1.-
  N5: B.anode, BR.Pin_1
  N6: G.anode, GR.Pin_1
  N7: U1.Trigger, U1.Threshold, R5.Pin_1, C1.+
  N8: U1.Output, RR.Pin_1, WR.Pin_1, BR.Pin_0, GR.Pin_0, R5.Pin_0
