# Fritzing sketch Arduino - GRBL Controller (saved by Fritzing 0.7.0b)
breadboards: 1

parts:
  U1 = atmega168 [package="DIP28 [THT]"]
  J1 = female pin header, 2 pins [form="♀ (female)"]
  XTAL1 = Crystal [frequency="16 Mhz" package=THT]
  C1 = Ceramic Capacitor [capacitance=100nF package="100 mil [THT, multilayer]"]
  C2 = Ceramic Capacitor [capacitance=100nF package="100 mil [THT, multilayer]"]
  LED1 = LED - 3mm [color="Red (633nm)" package="3 mm [THT]"]  # not connected
  R1 = Resistor [tolerance=±5% resistance=220 package=THT]
  R2 = Resistor [tolerance=±5% resistance=220 package=THT]  # not connected
  J2 = female pin header, 2 pins [form="♀ (female)"]
  J3 = female pin header, 2 pins [form="♀ (female)"]
  J4 = female pin header, 2 pins [form="♀ (female)"]

nets:
  N1: U1.Pin_1, R1.Pin_1
  N2: U1.Pin_2, J2.pin1
  N3: U1.Pin_3, J3.pin1
  N4: U1.Pin_4, J4.pin1
  N5: U1.Pin_5, J2.pin2
  N6: U1.Pin_6, J3.pin2
  N7: U1.Pin_7, U1.Pin_20, U1.Pin_21, J1.pin1, R1.Pin_0
  N8: U1.Pin_8, U1.Pin_22, J1.pin2, C1.0, C2.0
  N9: U1.Pin_9, XTAL1.pin_0, C1.1
  N10: U1.Pin_10, XTAL1.pin_1, C2.1
  N11: U1.Pin_11, J4.pin2
