# Fritzing sketch Arduino ATMega8A (saved by Fritzing 0.7.1b)
breadboards: 1

parts:
  IC1 = TQFP32-5MM [chip_label=IC spacing=300mil package=TQFP]
  U1 = Voltage Regulator - 5V [package="TO220 [THT]"]
  J1 = female pin header, 2 pins [form="♀ (female)"]
  J2 = female pin header, 2 pins [form="♀ (female)"]
  POWER = smd LED [color="Red (633nm)" package="0805 [SMD]"]
  R1 = Resistor [tolerance=±5% resistance=220 package="0805 [SMD]"]
  XTAL1 = Crystal [frequency="16 Mhz" package=THT]
  C1 = Ceramic Capacitor [capacitance=100nF package="100 mil [THT, multilayer]"]
  C2 = Ceramic Capacitor [capacitance=100nF package="100 mil [THT, multilayer]"]
  C3 = Electrolytic Capacitor [capacitance=1µF package="100 mil [THT, electrolytic]"]
  C4 = Electrolytic Capacitor [capacitance=1µF package="100 mil [THT, electrolytic]"]

nets:
  N1: IC1.3, IC1.5, IC1.21, U1.GND, J1.pin2, J2.pin1, R1.Pin_0, C1.0, C2.0, C3.-, C4.-
  N2: IC1.4, IC1.6, IC1.18, IC1.20, U1.output_voltage, J2.pin2, POWER.cathode, C4.+
  N3: IC1.7, XTAL1.pin_0, C1.1
  N4: IC1.8, XTAL1.pin_1, C2.1
  N5: U1.input_voltage, J1.pin1, C3.+
  N6: POWER.anode, R1.Pin_1
