# Fritzing sketch Arduino ATMega8U (saved by Fritzing 0.7.0b)
breadboards: 1

parts:
  IC1 = TQFP32-5MM [chip_label=IC spacing=300mil package=TQFP]
  XTAL1 = Crystal [frequency="16 Mhz" package=SMD]
  R1 = Resistor [tolerance=±5% resistance=10k package="0805 [SMD]"]
  J1 = female pin header, 6 pins [form="♀ (female)"]
  J2 = female pin header, 8 pins [form="♀ (female)"]
  J3 = female pin header, 8 pins [form="♀ (female)"]

nets:
  N1: IC1.1, XTAL1.pin_0
  N2: IC1.2, XTAL1.pin_1
  N3: IC1.3, J1.pin1
  N4: IC1.4, J1.pin2
  N5: IC1.5, J1.pin3
  N6: IC1.6, J1.pin4
  N7: IC1.7, J1.pin5
  N8: IC1.8, J1.pin6
  N9: IC1.9, J2.pin8
  N10: IC1.10, J2.pin7
  N11: IC1.11, J2.pin6
  N12: IC1.12, J2.pin5
  N13: IC1.13, J2.pin4
  N14: IC1.14, J2.pin3
  N15: IC1.15, J2.pin2
  N16: IC1.16, J2.pin1
  N17: IC1.17, J3.pin8
  N18: IC1.18, J3.pin7
  N19: IC1.19, J3.pin6
  N20: IC1.20, J3.pin5
  N21: IC1.21, J3.pin4
  N22: IC1.22, J3.pin3
  N23: IC1.23, J3.pin2
  N24: IC1.24, R1.Pin_0, J3.pin1
