# Fritzing sketch Arduino AVR ISP (saved by Fritzing 0.6.4b)
breadboards: 1

parts:
  U1 = atmega168 [package="DIP28 [THT]"]
  LED1 = smd LED [color="Red (633nm)" package="0805 [SMD]"]
  LED3 = smd LED [color="Red (633nm)" package="0805 [SMD]"]
  LED2 = smd LED [color="Red (633nm)" package="0805 [SMD]"]
  R2 = Resistor [tolerance=±5% resistance=220 package="0805 [SMD]"]
  R3 = Resistor [tolerance=±5% resistance=220 package="0805 [SMD]"]
  R4 = Resistor [tolerance=±5% resistance=220 package="0805 [SMD]"]
  R1 = Resistor [tolerance=±5% resistance=220 package="0805 [SMD]"]
  J3 = female pin header, 2 pins [form="♀ (female)"]
  J4 = female pin header, 2 pins [form="♀ (female)"]
  J5 = female pin header, 3 pins [form="♀ (female)"]
  J2 = male pin header, 12 pins [form="♂ (male)"]
  J1 = male pin header, 16 pins [form="♂ (male)"]

nets:
  N1: U1.Pin_1, R1.Pin_1, J1.pin6
  N2: U1.Pin_7, U1.Pin_20, R1.Pin_0, J2.pin3
  N3: U1.Pin_8, U1.Pin_22, J2.pin4, J1.pin2
  N4: U1.Pin_9, J4.pin1, J5.pin3
  N5: U1.Pin_10, J3.pin1, J5.pin1
  N6: U1.Pin_17, J1.pin5
  N7: U1.Pin_18, J1.pin4
  N8: U1.Pin_19, J1.pin3
  N9: LED1.cathode, J1.pin8
  N10: LED1.anode, R2.Pin_1
  N11: LED3.cathode, J1.pin9
  N12: LED3.anode, R3.Pin_1
  N13: LED2.cathode, J1.pin10
  N14: LED2.anode, R4.Pin_1
  N15: R2.Pin_0, R3.Pin_0, R4.Pin_0, J3.pin2, J4.pin2
