# Fritzing sketch Arduino Bare Bones - I2C - v3.fz (saved by Fritzing 0.7.0b)
breadboards: 1

parts:
  ATMega = atmega168 [package="DIP28 [THT]"]
  L7805 = Voltage Regulator - 5V [package="TO220 [THT]"]
  C1 = Electrolytic Capacitor [capacitance=10µF voltage=10V package="100 mil [THT, electrolytic]"]
  C2 = Electrolytic Capacitor [capacitance=10µF voltage=10V package="100 mil [THT, electrolytic]"]
  +VCC = smd LED [color="Red (633nm)" package="0805 [SMD]"]
  R1 = Resistor [tolerance=±5% resistance=330 package="0805 [SMD]"]
  R2 = Resistor [tolerance=±5% resistance=100 package="0805 [SMD]"]
  Blink = smd LED [color="Red (633nm)" package="0805 [SMD]"]
  R3 = Resistor [tolerance=±5% resistance=100 package="0805 [SMD]"]
  +5v = smd LED [color="Red (633nm)" package="0805 [SMD]"]
  R4 = Resistor [tolerance=±5% resistance=10k package="0805 [SMD]"]
  22pf = Ceramic Capacitor [capacitance=100nF package="0805 [SMD, multilayer]"]
  22pf_2 = Ceramic Capacitor [capacitance=100nF package="0805 [SMD, multilayer]"]
  XTAL1 = Crystal [frequency="16 Mhz" package=THT]
  AutoReset = Ceramic Capacitor [capacitance=0.1µF package="0805 [SMD, multilayer]"]
  +9V = female pin header, 2 pins [form="♀ (female)"]
  I2C_In = female pin header, 4 pins [form="♀ (female)"]
  I2C_out = female pin header, 4 pins [form="♀ (female)"]
  I2C_Master = female pin header, 2 pins [form="♀ (female)"]
  R5 = Resistor [tolerance=±5% resistance=4.7k package="0805 [SMD]"]
  R6 = Resistor [tolerance=±5% resistance=4.7k package="0805 [SMD]"]

nets:
  N1: ATMega.Pin_1, R4.Pin_1, AutoReset.1
  N2: ATMega.Pin_7, ATMega.Pin_20, ATMega.Pin_21, L7805.output_voltage, C1.+, +5v.anode, R4.Pin_0, I2C_Master.pin1
  N3: ATMega.Pin_8, ATMega.Pin_22, L7805.GND, C1.-, C2.-, R1.Pin_0, R2.Pin_0, R3.Pin_0, 22pf.0, 22pf_2.0, +9V.pin2
  N4: ATMega.Pin_9, 22pf.1, XTAL1.pin_0
  N5: ATMega.Pin_10, 22pf_2.1, XTAL1.pin_1
  N6: ATMega.Pin_19, Blink.cathode
  N7: ATMega.Pin_27, I2C_In.pin1, I2C_out.pin1, R6.Pin_0
  N8: ATMega.Pin_28, I2C_In.pin2, I2C_out.pin2, R5.Pin_1
  N9: L7805.input_voltage, C2.+, +VCC.anode, +9V.pin1
  N10: +VCC.cathode, R1.Pin_1
  N11: R2.Pin_1, Blink.anode
  N12: R3.Pin_1, +5v.cathode
  N13: I2C_In.pin3, I2C_out.pin3
  N14: I2C_In.pin4, I2C_out.pin4
  N15: I2C_Master.pin2, R5.Pin_0, R6.Pin_1
