# Fritzing sketch Arduino Bare Bones - v2 (saved by Fritzing 0.6.4b)
breadboards: 1

parts:
  Arduino_ATMega328 = atmega168 [package="DIP28 [THT]"]
  16Mhz = Crystal [frequency="16 Mhz" package=THT]
  VR1 = Voltage Regulator - 5V [package="TO220 [THT]"]
  C3 = Electrolytic Capacitor [capacitance=10µF voltage=16V package="100 mil [THT, electrolytic]"]
  C4 = Electrolytic Capacitor [capacitance=10µF voltage=16V package="100 mil [THT, electrolytic]"]
  R1 = Resistor [tolerance=±5% resistance=10k package=THT]
  J3 = female pin header, 5 pins [form="♀ (female)"]
  C2 = Ceramic Capacitor [capacitance=22pF voltage=35V package="200 mil [THT, multilayer]"]
  J6 = male pin header, 6 pins [form="♂ (male)"]
  J5 = male pin header, 5 pins [form="♂ (male)"]
  J4 = male pin header, 4 pins [form="♂ (male)"]
  +9V = male pin header, 2 pins [form="♂ (male)"]
  +5V = male pin header, 2 pins [form="♂ (male)"]
  USB = female pin header, 5 pins [form="♀ (female)"]
  C5 = Ceramic Capacitor [capacitance=0.1µF voltage=10V package="100 mil [THT, multilayer]"]
  BLINK = smd LED [color="Red (633nm)" package="0805 [SMD]"]
  R3 = Resistor [tolerance=±5% resistance=100 package="0805 [SMD]"]
  R2 = Resistor [tolerance=±5% resistance=100 package="0805 [SMD]"]
  POWER = smd LED [color="Red (633nm)" package="0805 [SMD]"]
  C1 = Ceramic Capacitor [capacitance=22pF voltage=35V package="200 mil [THT, multilayer]"]
  J7 = male pin header, 4 pins [form="♂ (male)"]  # not connected
  J8 = male pin header, 4 pins [form="♂ (male)"]
  Auto_reset = male pin header, 2 pins [form="♂ (male)"]

nets:
  N1: Arduino_ATMega328.Pin_1, R1.Pin_1, C5.0
  N2: Arduino_ATMega328.Pin_2, J3.pin1, USB.pin2
  N3: Arduino_ATMega328.Pin_3, J3.pin2, USB.pin3
  N4: Arduino_ATMega328.Pin_4, J3.pin3
  N5: Arduino_ATMega328.Pin_5, J3.pin4
  N6: Arduino_ATMega328.Pin_6, J3.pin5
  N7: Arduino_ATMega328.Pin_7, Arduino_ATMega328.Pin_20, Arduino_ATMega328.Pin_21, VR1.output_voltage, C3.+, R1.Pin_0, +5V.pin2, USB.pin5, POWER.cathode
  N8: Arduino_ATMega328.Pin_8, Arduino_ATMega328.Pin_22
  N9: Arduino_ATMega328.Pin_9, 16Mhz.pin_0, C1.1
  N10: Arduino_ATMega328.Pin_10, 16Mhz.pin_1, C2.1
  N11: Arduino_ATMega328.Pin_11, J4.pin1
  N12: Arduino_ATMega328.Pin_12, J4.pin2
  N13: Arduino_ATMega328.Pin_13, J4.pin3
  N14: Arduino_ATMega328.Pin_14, J4.pin4
  N15: Arduino_ATMega328.Pin_15, J5.pin5
  N16: Arduino_ATMega328.Pin_16, J5.pin4
  N17: Arduino_ATMega328.Pin_17, J5.pin3
  N18: Arduino_ATMega328.Pin_18, J5.pin2
  N19: Arduino_ATMega328.Pin_19, J5.pin1, BLINK.anode
  N20: Arduino_ATMega328.Pin_23, J6.pin6
  N21: Arduino_ATMega328.Pin_24, J6.pin5
  N22: Arduino_ATMega328.Pin_25, J6.pin4
  N23: Arduino_ATMega328.Pin_26, J6.pin3
  N24: Arduino_ATMega328.Pin_27, J6.pin2
  N25: Arduino_ATMega328.Pin_28, J6.pin1
  N26: VR1.input_voltage, C4.+, +9V.pin1
  N27: VR1.GND, C3.-, C4.-, C2.0, +9V.pin2, +5V.pin1, USB.pin4, R3.Pin_0, R2.Pin_0, C1.0
  N28: USB.pin1, C5.1, Auto_reset.pin2
  N29: BLINK.cathode, R3.Pin_1
  N30: R2.Pin_1, POWER.anode
  N31: J8.pin1, Auto_reset.pin1

notes:
  AI5
  AI4
  AI3
  AI2
  AI1
  AI0
  D13
  D12
  D11(PWM)
  D10(PWM)
  D9(PWM)
  (PWM)D5
  (PWM)D6
  D7
  D8
  (RX)D0
  (TX)D1
  D2
  (PWM)D3
  D4
  RESET
  RST
  RXD
  GND
  TXD
  +5V
