# Fritzing sketch Arduino Bare Bones - v3 (saved by Fritzing 0.6.4b)
breadboards: 1

parts:
  U1 = atmega168 [package="DIP28 [THT]"]
  U2 = Voltage Regulator - 5V [package="TO220 [THT]"]
  C1 = Electrolytic Capacitor [capacitance=1µF package="100 mil [THT, electrolytic]"]
  C2 = Electrolytic Capacitor [capacitance=1µF package="100 mil [THT, electrolytic]"]
  +VCC = smd LED [color="Red (633nm)" package="0805 [SMD]"]
  R1 = Resistor [tolerance=±5% resistance=330 package="0805 [SMD]"]
  R2 = Resistor [tolerance=±5% resistance=100 package="0805 [SMD]"]
  Blink = smd LED [color="Red (633nm)" package="0805 [SMD]"]
  R3 = Resistor [tolerance=±5% resistance=100 package="0805 [SMD]"]
  +5v = smd LED [color="Red (633nm)" package="0805 [SMD]"]
  part = Resistor [tolerance=±5% resistance=10k package="0805 [SMD]"]
  22pf = Ceramic Capacitor [capacitance=100nF package="0805 [SMD, multilayer]"]
  22pf_2 = Ceramic Capacitor [capacitance=100nF package="0805 [SMD, multilayer]"]
  XTAL1 = Crystal [frequency="16 Mhz" package=THT]
  AutoReset = Ceramic Capacitor [capacitance=0.1µF package="0805 [SMD, multilayer]"]
  J2 = female pin header, 2 pins [form="♀ (female)"]

nets:
  N1: U1.Pin_1, part.Pin_1, AutoReset.1
  N2: U1.Pin_7, U1.Pin_20, U1.Pin_21, U2.output_voltage, C1.+, +5v.anode, part.Pin_0
  N3: U1.Pin_8, U1.Pin_22, U2.GND, C1.-, C2.-, R1.Pin_0, R2.Pin_0, R3.Pin_0, 22pf.0, 22pf_2.0, J2.pin2
  N4: U1.Pin_9, 22pf.1, XTAL1.pin_0
  N5: U1.Pin_10, 22pf_2.1, XTAL1.pin_1
  N6: U1.Pin_19, Blink.cathode
  N7: U2.input_voltage, C2.+, +VCC.anode, J2.pin1
  N8: +VCC.cathode, R1.Pin_1
  N9: R2.Pin_1, Blink.anode
  N10: R3.Pin_1, +5v.cathode
