# Fritzing sketch Arduino Bare Bones ATMega8L- SMD (saved by Fritzing 0.6.4b)
breadboards: 1

parts:
  U1 = atmega168 [package="DIP28 [THT]"]
  J1 = female pin header, 5 pins [form="♀ (female)"]
  J2 = female pin header, 6 pins [form="♀ (female)"]
  J3 = female pin header, 5 pins [form="♀ (female)"]
  J4 = female pin header, 4 pins [form="♀ (female)"]
  U2 = Voltage Regulator - 5V [package="TO220 [THT]"]
  R1 = Resistor [tolerance=±5% resistance=220 package=THT]
  S1 = Pushbutton [package="[THT]"]
  C1 = Electrolytic Capacitor [capacitance=1µF package="100 mil [THT, electrolytic]"]
  C2 = Electrolytic Capacitor [capacitance=1µF package="100 mil [THT, electrolytic]"]
  J5 = female pin header, 2 pins [form="♀ (female)"]
  J6 = female pin header, 4 pins [form="♀ (female)"]
  POWER = smd LED [color="Red (633nm)" package="0805 [SMD]"]
  R2 = Resistor [tolerance=±5% resistance=220 package="0805 [SMD]"]
  BLINK = smd LED [color="Red (633nm)" package="0805 [SMD]"]
  R3 = Resistor [tolerance=±5% resistance=220 package="0805 [SMD]"]
  LED1 = smd LED [color="Red (633nm)" package="0805 [SMD]"]
  R4 = Resistor [tolerance=±5% resistance=220 package="0805 [SMD]"]
  C3 = Ceramic Capacitor [capacitance=100nF package="100 mil [THT, multilayer]"]
  C4 = Ceramic Capacitor [capacitance=100nF package="100 mil [THT, multilayer]"]

nets:
  N1: U1.Pin_1, R1.Pin_1
  N2: U1.Pin_2, J1.pin1, J6.pin1, LED1.cathode
  N3: U1.Pin_3, J1.pin2, J6.pin2
  N4: U1.Pin_4, J1.pin3
  N5: U1.Pin_5, J1.pin4
  N6: U1.Pin_6, J1.pin5
  N7: U1.Pin_7, U1.Pin_20, U1.Pin_21, U2.output_voltage, R1.Pin_0, C2.+, J6.pin4, POWER.cathode, R4.Pin_0
  N8: U1.Pin_8, U1.Pin_22, R2.Pin_0, R3.Pin_0, C3.0, C4.0
  N9: U1.Pin_9, C4.1
  N10: U1.Pin_10, C3.1
  N11: U1.Pin_11, J4.pin1
  N12: U1.Pin_12, J4.pin2
  N13: U1.Pin_13, J4.pin3
  N14: U1.Pin_14, J4.pin4
  N15: U1.Pin_15, J3.pin5
  N16: U1.Pin_16, J3.pin4
  N17: U1.Pin_17, J3.pin3
  N18: U1.Pin_18, J3.pin2
  N19: U1.Pin_19, J3.pin1, BLINK.cathode
  N20: U1.Pin_23, J2.pin6
  N21: U1.Pin_24, J2.pin5
  N22: U1.Pin_25, J2.pin4
  N23: U1.Pin_26, J2.pin3
  N24: U1.Pin_27, J2.pin2
  N25: U1.Pin_28, J2.pin1
  N26: U2.input_voltage, C1.+, J5.pin1
  N27: U2.GND, S1.Pin_3, S1.Pin_4, C1.-, C2.-, J5.pin2, J6.pin3
  N28: POWER.anode, R2.Pin_1
  N29: BLINK.anode, R3.Pin_1
  N30: LED1.anode, R4.Pin_1
