# Fritzing sketch Arduino Stepper Driver (saved by Fritzing 0.7.1b)
breadboards: 1

parts:
  L298N1 = L298N
  U1 = atmega168 [package=dip]
  XTAL1 = Crystal [frequency="16 Mhz" package=THT]
  J1 = female pin header, 5 pins [form="♀ (female)"]
  R1 = Resistor [tolerance=±5% resistance=10k package=THT]
  R2 = Resistor [tolerance=±5% resistance=1 package=THT]
  R3 = Resistor [tolerance=±5% resistance=1 package=THT]
  D1 = Rectifier Diode [part_number=1N4001 package="300 mil [THT]"]
  D2 = Rectifier Diode [part_number=1N4001 package="300 mil [THT]"]
  D3 = Rectifier Diode [part_number=1N4001 package="300 mil [THT]"]
  D4 = Rectifier Diode [part_number=1N4001 package="300 mil [THT]"]
  D5 = Rectifier Diode [part_number=1N4001 package="300 mil [THT]"]
  D6 = Rectifier Diode [part_number=1N4001 package="300 mil [THT]"]
  D7 = Rectifier Diode [part_number=1N4001 package="300 mil [THT]"]
  D8 = Rectifier Diode [part_number=1N4001 package="300 mil [THT]"]
  R4 = Resistor [tolerance=±5% resistance=220 package=THT]
  C1 = Ceramic Capacitor [capacitance=10pF voltage=16V package="100 mil [THT, multilayer]"]
  C2 = Ceramic Capacitor [capacitance=10pF voltage=16V package="100 mil [THT, multilayer]"]
  R5 = Resistor [tolerance=±5% resistance=220 package=THT]
  LED2 = LED - 3mm [color="Red (633nm)" package="3 mm [THT]"]
  LED1 = LED - 3mm [color="Red (633nm)" package="3 mm [THT]"]
  J3 = screw terminal, 2 pins
  J2 = screw terminal, 4 pins
  LED3 = LED - 3mm [color="Red (633nm)" package="3 mm [THT]"]
  R6 = Resistor [tolerance=±5% resistance=220 package=THT]

nets:
  N1: L298N1.C1, R2.Pin_1
  N2: L298N1.C2, D4.anode, D5.cathode, J2.pin1
  N3: L298N1.C3, D1.anode, D6.cathode, J2.pin2
  N4: L298N1.C4, D1.cathode, D2.cathode, D3.cathode, D4.cathode, LED1.anode, J3.pin1
  N5: L298N1.C5, U1.D13
  N6: L298N1.C6, L298N1.C11, U1.D11_(PWM)
  N7: L298N1.C7, U1.D12
  GND: L298N1.C8, U1.GND, J1.pin2, R2.Pin_0, R3.Pin_1, D5.anode, D6.anode, D7.anode, D8.anode, R4.Pin_1, C1.0, C2.0, R5.Pin_0, J3.pin2, R6.Pin_0
  5V: L298N1.C9, U1.VCC, U1.AVCC, U1.AREF, J1.pin1, R1.Pin_0
  N8: L298N1.C10, U1.D10_(PWM)
  N9: L298N1.C12, U1.D9_(PWM)
  N10: L298N1.C13, D2.anode, D7.cathode, J2.pin3
  N11: L298N1.C14, D3.anode, D8.cathode, J2.pin4
  N12: L298N1.C15, R3.Pin_0
  N13: U1.RESET, R1.Pin_1
  N14: U1.D2, J1.pin3, LED2.anode
  N15: U1.D3_(PWM), J1.pin4
  N16: U1.D4, J1.pin5
  N17: U1.XLAT1, XTAL1.pin_0, C1.1
  N18: U1.XLAT2, XTAL1.pin_1, C2.1
  N19: U1.D7, LED3.cathode
  N20: R4.Pin_0, LED1.cathode
  N21: R5.Pin_1, LED2.cathode
  N22: LED3.anode, R6.Pin_1
