# Fritzing sketch BlinkM-atmega8a (saved by Fritzing 0.7.0b)
breadboards: 1

parts:
  IC1 = LQFP-32 [chip_label=IC spacing=300mil package=LQFP]
  LED1 = RGB LED (com. cathode, rbg) [package="5 mm [THT]"]
  R1 = Resistor [tolerance=±5% resistance=220 package="0805 [SMD]"]
  R2 = Resistor [tolerance=±5% resistance=220 package="0805 [SMD]"]
  R3 = Resistor [tolerance=±5% resistance=220 package="0805 [SMD]"]

nets:
  N1: IC1.3, IC1.5, IC1.21, LED1.common_cathode
  N2: IC1.4, IC1.6, IC1.18, IC1.20
  N3: IC1.13, R1.Pin_1
  N4: IC1.14, R3.Pin_1
  N5: IC1.15, R2.Pin_1
  N6: LED1.red_anode, R1.Pin_0
  N7: LED1.blue_anode, R3.Pin_0
  N8: LED1.green_anode, R2.Pin_0
