# Fritzing sketch BreadBoard Arduino (saved by Fritzing 0.7.0b)
breadboards: 1

parts:
  U1 = atmega168 [package="DIP28 [THT]"]
  Y1 = Resonator [frequency="16 Mhz" package=THT]
  U2 = Voltage Regulator - 5V [package="TO220 [THT]"]
  LED1 = LED - 5mm [color="Red (633nm)" package="5 mm [THT]"]
  C1 = Electrolytic Capacitor [capacitance=1µF package="100 mil [THT, electrolytic]"]
  C2 = Electrolytic Capacitor [capacitance=1µF package="100 mil [THT, electrolytic]"]
  R1 = Resistor [tolerance=±5% resistance=220 package=THT]
  J1 = female pin header, 14 pins [form="♀ (female)"]
  J2 = female pin header, 14 pins [form="♀ (female)"]
  R2 = Resistor [tolerance=±5% resistance=220 package=THT]
  S1 = Pushbutton [package="[THT]"]
  J3 = female pin header, 2 pins [form="♀ (female)"]

nets:
  GND: U1.Pin_1, U1.Pin_8, U1.Pin_22, Y1.GND, U2.GND, C1.-, C2.-, R1.Pin_1, J1.pin8, J2.pin7, R2.Pin_1, S1.Pin_3, S1.Pin_4, J3.pin1
  N1: U1.Pin_2, J1.pin2
  N2: U1.Pin_3, J1.pin3
  N3: U1.Pin_4, J1.pin4
  N4: U1.Pin_5, J1.pin5
  N5: U1.Pin_6, J1.pin6
  N6: U1.Pin_7, U1.Pin_20, U1.Pin_21, U2.output_voltage, C1.+, J1.pin7, R2.Pin_0
  N7: U1.Pin_9, Y1.0
  N8: U1.Pin_10, Y1.pin_1
  N9: U1.Pin_11, J1.pin11
  N10: U1.Pin_12, J1.pin12
  N11: U1.Pin_13, J1.pin13
  N12: U1.Pin_14, J1.pin14
  N13: U1.Pin_15, J2.pin14
  N14: U1.Pin_16, J2.pin13
  N15: U1.Pin_17, J2.pin12
  N16: U1.Pin_18, J2.pin11
  N17: U1.Pin_19, J2.pin10
  N18: U1.Pin_23, J2.pin6
  N19: U1.Pin_24, J2.pin5
  N20: U1.Pin_25, J2.pin4
  N21: U1.Pin_26, J2.pin3
  N22: U1.Pin_27, J2.pin2
  N23: U1.Pin_28, J2.pin1
  N24: U2.input_voltage, LED1.anode, C2.+, J3.pin2
  N25: LED1.cathode, R1.Pin_0
