# Fritzing sketch CapSense (saved by Fritzing 0.7.1b)
breadboards: 1

parts:
  Pad1 = Pad [width=30 height=30 connect=north]  # not connected
  R1 = Resistor [tolerance=±5% resistance=220 package=THT]
  R2 = Resistor [tolerance=±5% resistance=220 package=THT]
  R3 = Resistor [tolerance=±5% resistance=220 package=THT]
  R4 = Resistor [tolerance=±5% resistance=220 package=THT]
  Pad2 = Pad [width=30 height=30 connect=north]  # not connected
  R5 = Resistor [tolerance=±5% resistance=220 package=THT]
  R6 = Resistor [tolerance=±5% resistance=220 package=THT]
  Pad3 = Pad [width=30 height=30 connect=north]  # not connected
  J1 = female pin header, 4 pins [form="♀ (female)"]

nets:
  N1: R1.Pin_0, R3.Pin_0, R5.Pin_0, J1.pin1
  N2: R2.Pin_0, J1.pin4
  N3: R4.Pin_0, J1.pin3
  N4: R6.Pin_0, J1.pin2
