# Fritzing sketch Colour Sensor - v1 (saved by Fritzing 0.6.4b)
breadboards: 1

parts:
  R1 = Resistor [tolerance=±5% resistance=220 package=THT]
  CDS = Photocell (LDR) [package=THT]
  RGB = RGB LED (com. cathode, rbg) [package="5 mm [THT]"]
  J1 = female pin header, 6 pins [form="♀ (female)"]
  R3 = Resistor [tolerance=±5% resistance=10k package=THT]

nets:
  N1: R1.Pin_0, RGB.common_cathode
  N2: R1.Pin_1, J1.pin1, R3.Pin_1
  N3: CDS.pin_0, J1.pin3, R3.Pin_0
  N4: CDS.pin_1, J1.pin2
  N5: RGB.red_anode, J1.pin4
  N6: RGB.blue_anode, J1.pin6
  N7: RGB.green_anode, J1.pin5
