# Fritzing sketch L297-8 Stepper Driver (saved by Fritzing 0.7.1b)
breadboards: 1

parts:
  L298N1 = L298N
  J1 = female pin header, 5 pins [form="♀ (female)"]
  J2 = screw terminal, 4 pins
  J3 = Screw terminal - 2 pins [package=THT]
  R2 = Resistor [tolerance=±5% resistance=1 package=THT]
  R3 = Resistor [tolerance=±5% resistance=1 package=THT]
  D1 = Rectifier Diode [part_number=1N4001 package="300 mil [THT]"]
  D2 = Rectifier Diode [part_number=1N4001 package="300 mil [THT]"]
  D3 = Rectifier Diode [part_number=1N4001 package="300 mil [THT]"]
  D4 = Rectifier Diode [part_number=1N4001 package="300 mil [THT]"]
  D5 = Rectifier Diode [part_number=1N4001 package="300 mil [THT]"]
  D6 = Rectifier Diode [part_number=1N4001 package="300 mil [THT]"]
  D7 = Rectifier Diode [part_number=1N4001 package="300 mil [THT]"]
  D8 = Rectifier Diode [part_number=1N4001 package="300 mil [THT]"]
  LED1 = LED - 5mm [color="Red (633nm)" package="5 mm [THT]"]
  R4 = Resistor [tolerance=±5% resistance=220 package=THT]
  L297 = IC, DIP package, 20 pins [chip_label=IC spacing=300mil]
  R5 = Resistor [tolerance=±5% resistance=220 package=THT]
  C1 = Ceramic Capacitor [capacitance=3.3nF package="100 mil [THT, multilayer]"]

nets:
  N1: L298N1.C1, R2.Pin_1
  N2: L298N1.C2, J2.pin1, D4.anode, D5.cathode
  N3: L298N1.C3, J2.pin2, D1.anode, D6.cathode
  N4: L298N1.C4, J3.pin1, D1.cathode, D2.cathode, D3.cathode, D4.cathode, LED1.anode
  N5: L298N1.C5, L297.pin4
  N6: L298N1.C6, L298N1.C11
  N7: L298N1.C7, L297.pin6
  GND: L298N1.C8, J1.pin2, J3.pin2, R2.Pin_0, R3.Pin_1, D5.anode, D6.anode, D7.anode, D8.anode, L297.pin2, C1.0
  5V: L298N1.C9, J1.pin1, L297.pin12, R5.Pin_0
  N8: L298N1.C10, L297.pin7
  N9: L298N1.C12, L297.pin9
  N10: L298N1.C13, J2.pin3, D2.anode, D7.cathode
  N11: L298N1.C14, J2.pin4, D3.anode, D8.cathode
  N12: L298N1.C15, R3.Pin_0
  N13: J1.pin3, L297.pin17
  N14: J1.pin4, L297.pin18
  N15: J1.pin5, L297.pin10
  N16: LED1.cathode, R4.Pin_0
  N17: L297.pin16, R5.Pin_1, C1.1
