# Fritzing sketch LED Matrix 2 (saved by Fritzing 0.6.4b)
breadboards: 1

parts:
  LED2 = LED - 5mm [color="Red (633nm)" package="5 mm [THT]"]
  LED3 = LED - 5mm [color="Red (633nm)" package="5 mm [THT]"]  # not connected
  LED4 = LED - 5mm [color="Red (633nm)" package="5 mm [THT]"]  # not connected
  LED5 = LED - 5mm [color="Red (633nm)" package="5 mm [THT]"]  # not connected
  LED6 = LED - 5mm [color="Red (633nm)" package="5 mm [THT]"]  # not connected
  LED7 = LED - 5mm [color="Red (633nm)" package="5 mm [THT]"]  # not connected
  LED8 = LED - 5mm [color="Red (633nm)" package="5 mm [THT]"]  # not connected
  LED9 = LED - 5mm [color="Red (633nm)" package="5 mm [THT]"]
  LED10 = LED - 5mm [color="Red (633nm)" package="5 mm [THT]"]
  LED11 = LED - 5mm [color="Red (633nm)" package="5 mm [THT]"]  # not connected
  LED12 = LED - 5mm [color="Red (633nm)" package="5 mm [THT]"]  # not connected
  LED13 = LED - 5mm [color="Red (633nm)" package="5 mm [THT]"]  # not connected
  LED14 = LED - 5mm [color="Red (633nm)" package="5 mm [THT]"]  # not connected
  LED15 = LED - 5mm [color="Red (633nm)" package="5 mm [THT]"]  # not connected
  LED16 = LED - 5mm [color="Red (633nm)" package="5 mm [THT]"]  # not connected
  LED17 = LED - 5mm [color="Red (633nm)" package="5 mm [THT]"]
  LED18 = LED - 5mm [color="Red (633nm)" package="5 mm [THT]"]  # not connected
  LED19 = LED - 5mm [color="Red (633nm)" package="5 mm [THT]"]  # not connected
  LED20 = LED - 5mm [color="Red (633nm)" package="5 mm [THT]"]  # not connected
  LED21 = LED - 5mm [color="Red (633nm)" package="5 mm [THT]"]  # not connected
  LED22 = LED - 5mm [color="Red (633nm)" package="5 mm [THT]"]  # not connected
  LED23 = LED - 5mm [color="Red (633nm)" package="5 mm [THT]"]  # not connected
  LED24 = LED - 5mm [color="Red (633nm)" package="5 mm [THT]"]  # not connected
  LED25 = LED - 5mm [color="Red (633nm)" package="5 mm [THT]"]  # not connected
  LED26 = LED - 5mm [color="Red (633nm)" package="5 mm [THT]"]
  LED27 = LED - 5mm [color="Red (633nm)" package="5 mm [THT]"]  # not connected
  LED28 = LED - 5mm [color="Red (633nm)" package="5 mm [THT]"]  # not connected
  LED29 = LED - 5mm [color="Red (633nm)" package="5 mm [THT]"]  # not connected
  LED30 = LED - 5mm [color="Red (633nm)" package="5 mm [THT]"]  # not connected
  LED31 = LED - 5mm [color="Red (633nm)" package="5 mm [THT]"]  # not connected
  LED32 = LED - 5mm [color="Red (633nm)" package="5 mm [THT]"]  # not connected
  LED33 = LED - 5mm [color="Red (633nm)" package="5 mm [THT]"]
  LED34 = LED - 5mm [color="Red (633nm)" package="5 mm [THT]"]
  LED35 = LED - 5mm [color="Red (633nm)" package="5 mm [THT]"]  # not connected
  LED36 = LED - 5mm [color="Red (633nm)" package="5 mm [THT]"]  # not connected
  LED37 = LED - 5mm [color="Red (633nm)" package="5 mm [THT]"]  # not connected
  LED38 = LED - 5mm [color="Red (633nm)" package="5 mm [THT]"]  # not connected
  LED39 = LED - 5mm [color="Red (633nm)" package="5 mm [THT]"]  # not connected
  LED40 = LED - 5mm [color="Red (633nm)" package="5 mm [THT]"]  # not connected
  LED41 = LED - 5mm [color="Red (633nm)" package="5 mm [THT]"]
  LED42 = LED - 5mm [color="Red (633nm)" package="5 mm [THT]"]
  LED43 = LED - 5mm [color="Red (633nm)" package="5 mm [THT]"]  # not connected
  LED44 = LED - 5mm [color="Red (633nm)" package="5 mm [THT]"]  # not connected
  LED45 = LED - 5mm [color="Red (633nm)" package="5 mm [THT]"]  # not connected
  LED46 = LED - 5mm [color="Red (633nm)" package="5 mm [THT]"]  # not connected
  LED47 = LED - 5mm [color="Red (633nm)" package="5 mm [THT]"]  # not connected
  LED48 = LED - 5mm [color="Red (633nm)" package="5 mm [THT]"]  # not connected
  LED49 = LED - 5mm [color="Red (633nm)" package="5 mm [THT]"]
  LED50 = LED - 5mm [color="Red (633nm)" package="5 mm [THT]"]
  LED51 = LED - 5mm [color="Red (633nm)" package="5 mm [THT]"]  # not connected
  LED52 = LED - 5mm [color="Red (633nm)" package="5 mm [THT]"]  # not connected
  LED53 = LED - 5mm [color="Red (633nm)" package="5 mm [THT]"]  # not connected
  LED54 = LED - 5mm [color="Red (633nm)" package="5 mm [THT]"]  # not connected
  LED55 = LED - 5mm [color="Red (633nm)" package="5 mm [THT]"]  # not connected
  LED56 = LED - 5mm [color="Red (633nm)" package="5 mm [THT]"]  # not connected
  LED57 = LED - 5mm [color="Red (633nm)" package="5 mm [THT]"]
  LED58 = LED - 5mm [color="Red (633nm)" package="5 mm [THT]"]
  LED59 = LED - 5mm [color="Red (633nm)" package="5 mm [THT]"]
  LED60 = LED - 5mm [color="Red (633nm)" package="5 mm [THT]"]
  LED61 = LED - 5mm [color="Red (633nm)" package="5 mm [THT]"]
  LED62 = LED - 5mm [color="Red (633nm)" package="5 mm [THT]"]
  LED63 = LED - 5mm [color="Red (633nm)" package="5 mm [THT]"]
  LED64 = LED - 5mm [color="Red (633nm)" package="5 mm [THT]"]
  LED65 = LED - 5mm [color="Red (633nm)" package="5 mm [THT]"]
  R1 = Resistor [tolerance=±5% resistance=220 package=THT]
  R2 = Resistor [tolerance=±5% resistance=220 package=THT]
  R3 = Resistor [tolerance=±5% resistance=220 package=THT]
  R4 = Resistor [tolerance=±5% resistance=220 package=THT]
  R5 = Resistor [tolerance=±5% resistance=220 package=THT]
  R6 = Resistor [tolerance=±5% resistance=220 package=THT]
  R7 = Resistor [tolerance=±5% resistance=220 package=THT]
  R8 = Resistor [tolerance=±5% resistance=220 package=THT]
  U1 = 74HC595 [package="DIP16 [THT]"]
  IC1 = ULN2803A [package=THT]

nets:
  N1: LED2.cathode, LED9.cathode
  N2: LED10.cathode, LED17.cathode
  N3: LED26.cathode, LED33.cathode
  N4: LED34.cathode, LED41.cathode
  N5: LED42.cathode, LED49.cathode
  N6: LED50.cathode, LED57.cathode
  N7: LED58.cathode, LED65.cathode
  N8: LED58.anode, R1.Pin_0
  N9: LED59.anode, R4.Pin_0
  N10: LED60.anode, R3.Pin_0
  N11: LED61.anode, R2.Pin_0
  N12: LED62.anode, R5.Pin_0
  N13: LED63.anode, R8.Pin_0
  N14: LED64.anode, R6.Pin_0
  N15: LED65.anode, R7.Pin_0
  N16: R1.Pin_1, IC1.Out_1
  N17: R2.Pin_1, IC1.Out_4
  N18: R3.Pin_1, IC1.Out_3
  N19: R4.Pin_1, IC1.Out_2
  N20: R5.Pin_1, IC1.Out_5
  N21: R6.Pin_1, IC1.Out_7
  N22: R7.Pin_1, IC1.Out_8
  N23: R8.Pin_1, IC1.Out_6
  N24: U1.Q1, IC1.In_7
  N25: U1.Q2, IC1.In_6
  N26: U1.Q3, IC1.In_5
  N27: U1.Q4, IC1.In_4
  N28: U1.Q5, IC1.In_3
  N29: U1.Q6, IC1.In_2
  N30: U1.Q7, IC1.In_1
  N31: U1.VCC, IC1.In_8
