# Fritzing sketch Laser DDL (saved by Fritzing 0.7.1b)
breadboards: 1

parts:
  LM317 = Voltage Regulator - Variable [package="TO220 [THT]"]
  LASER = female pin header, 2 pins [form="♀ (female)"]
  R1 = Rotary Potentiometer (Small) [maximum_resistance=0.1MΩ]
  R2 = Resistor [tolerance=±5% resistance=10 package=THT]
  R3 = Resistor [tolerance=±5% resistance=10 package=THT]
  D1 = Rectifier Diode [part_number=1N4001 package="300 mil [THT]"]
  C1 = Electrolytic Capacitor [capacitance=10µF voltage=16V package="100 mil [THT, electrolytic]"]
  Q1 = NPN-Transistor [package="TO92 [THT]"]
  +7_2 = female pin header, 3 pins [form="♀ (female)"]
  R4 = Resistor [tolerance=±5% resistance=220 package=THT]

nets:
  N1: LM317.ADJ, LASER.pin1, R2.Pin_0, R3.Pin_0, D1.anode, C1.+
  N2: LM317.OUT, R1.leg2
  N3: LM317.IN, +7_2.pin1
  N4: LASER.pin2, D1.cathode, C1.-, Q1.E
  N5: R1.leg1, R1.wiper, R2.Pin_1, R3.Pin_1
  N6: Q1.B, R4.Pin_1
  N7: Q1.C, +7_2.pin2
  N8: +7_2.pin3, R4.Pin_0
