# Fritzing sketch Light Module - NPN - 8ch (saved by Fritzing 0.6.4b)
breadboards: 1

parts:
  U1 = 74HC595 [package="DIP16 [THT]"]
  R1 = Resistor [tolerance=±5% resistance=220 package=THT]
  R2 = Resistor [tolerance=±5% resistance=220 package=THT]
  R3 = Resistor [tolerance=±5% resistance=220 package=THT]
  R4 = Resistor [tolerance=±5% resistance=220 package=THT]
  R5 = Resistor [tolerance=±5% resistance=220 package=THT]
  R6 = Resistor [tolerance=±5% resistance=220 package=THT]
  R7 = Resistor [tolerance=±5% resistance=220 package=THT]
  R8 = Resistor [tolerance=±5% resistance=220 package=THT]
  Light_0 = female pin header, 2 pins [form="♀ (female)"]
  Light_1 = female pin header, 2 pins [form="♀ (female)"]
  Light_2 = female pin header, 2 pins [form="♀ (female)"]
  Light_3 = female pin header, 2 pins [form="♀ (female)"]
  Light_4 = female pin header, 2 pins [form="♀ (female)"]
  Light_5 = female pin header, 2 pins [form="♀ (female)"]
  Light_6 = female pin header, 2 pins [form="♀ (female)"]
  Light_7 = female pin header, 2 pins [form="♀ (female)"]
  Q1 = NPN-Transistor [package="TO92 [THT]"]
  R9 = Resistor [tolerance=±5% resistance=220 package=THT]
  Q2 = NPN-Transistor [package="TO92 [THT]"]
  Q3 = NPN-Transistor [package="TO92 [THT]"]
  Q4 = NPN-Transistor [package="TO92 [THT]"]
  Q5 = NPN-Transistor [package="TO92 [THT]"]
  Q6 = NPN-Transistor [package="TO92 [THT]"]
  Q7 = NPN-Transistor [package="TO92 [THT]"]
  Q8 = NPN-Transistor [package="TO92 [THT]"]
  R10 = Resistor [tolerance=±5% resistance=220 package=THT]
  R11 = Resistor [tolerance=±5% resistance=220 package=THT]
  R12 = Resistor [tolerance=±5% resistance=220 package=THT]
  R13 = Resistor [tolerance=±5% resistance=220 package=THT]
  R14 = Resistor [tolerance=±5% resistance=220 package=THT]
  R15 = Resistor [tolerance=±5% resistance=220 package=THT]
  R16 = Resistor [tolerance=±5% resistance=22 package=THT]
  Light_Supply_Power = Screw terminal - 2 pins [package=THT]
  R17 = Resistor [tolerance=±5% resistance=220 package=THT]
  LED1 = LED - 5mm [color="Red (633nm)" package="5 mm [THT]"]
  DC_ON = LED - 5mm [color="Red (633nm)" package="5 mm [THT]"]
  R18 = Resistor [tolerance=±5% resistance=220 package=THT]
  Data_In = RJ45
  Data_Out = RJ45
  Out = female pin header, 4 pins [form="♀ (female)"]
  In = female pin header, 4 pins [form="♀ (female)"]
  DC_Out = female pin header, 2 pins [form="♀ (female)"]
  DC_In = female pin header, 2 pins [form="♀ (female)"]
  DC_Power = female pin header, 2 pins [form="♀ (female)"]

nets (from the pcb view):
  N1: U1.Q1, R2.Pin_1
  N2: U1.Q2, R3.Pin_1
  N3: U1.Q3, R4.Pin_1
  N4: U1.Q4, R5.Pin_1
  N5: U1.Q5, R6.Pin_1
  N6: U1.Q6, R7.Pin_1
  N7: U1.Q7, R8.Pin_1
  N8: U1.GND, U1.OE, Q1.E, Q2.E, Q3.E, Q4.E, Q5.E, Q6.E, Q7.E, Q8.E, Light_Supply_Power.pin2, R17.Pin_1, R18.Pin_1, Data_Out.connector4, DC_Out.pin2, DC_Power.pin2
  N9: U1.MR, U1.VCC, DC_ON.anode, DC_Power.pin1
  N10: U1.Q0, R1.Pin_1
  N11: R1.Pin_0, Q1.B
  N12: R2.Pin_0, Q2.B
  N13: R3.Pin_0, Q3.B
  N14: R4.Pin_0, Q4.B
  N15: R5.Pin_0, Q6.B
  N16: R6.Pin_0, Q5.B
  N17: R7.Pin_0, Q7.B
  N18: R8.Pin_0, Q8.B
  N19: Light_0.pin1, Light_1.pin1, Light_2.pin1, Light_3.pin1, Light_4.pin1, Light_5.pin1, Light_6.pin1, Light_7.pin1, Light_Supply_Power.pin1, LED1.cathode
  N20: Light_0.pin2, R9.Pin_0
  N21: Light_1.pin2, R10.Pin_0
  N22: Light_2.pin2, R11.Pin_0
  N23: Light_3.pin2, R12.Pin_0
  N24: Light_4.pin2, R13.Pin_0
  N25: Light_5.pin2, R14.Pin_0
  N26: Light_6.pin2, R15.Pin_0
  N27: Light_7.pin2, R16.Pin_0
  N28: Q1.C, R9.Pin_1
  N29: Q2.C, R10.Pin_1
  N30: Q3.C, R11.Pin_1
  N31: Q4.C, R12.Pin_1
  N32: Q5.C, R14.Pin_1
  N33: Q6.C, R13.Pin_1
  N34: Q7.C, R15.Pin_1
  N35: Q8.C, R16.Pin_1
  N36: R17.Pin_0, LED1.anode
  N37: DC_ON.cathode, R18.Pin_0
  N38: Data_In.connector0, In.pin4
  N39: Data_In.connector2, In.pin3
  N40: Data_In.connector4, DC_In.pin2
  N41: Data_In.connector5, In.pin2
  N42: Data_In.connector6, DC_In.pin1
  N43: Data_In.connector7, In.pin1
  N44: Data_Out.connector0, Out.pin4
  N45: Data_Out.connector2, Out.pin3
  N46: Data_Out.connector5, Out.pin2
  N47: Data_Out.connector6, DC_Out.pin1
  N48: Data_Out.connector7, Out.pin1

notes:
  lights control board v1
