# Fritzing sketch Light Module - PWM- 16ch (saved by Fritzing 0.6.4b)
breadboards: 1

parts:
  U1 = atmega168 [package="DIP28 [THT]"]
  R2 = Resistor [tolerance=±5% resistance=220 package=THT]
  R3 = Resistor [tolerance=±5% resistance=220 package=THT]
  R4 = Resistor [tolerance=±5% resistance=220 package=THT]
  R5 = Resistor [tolerance=±5% resistance=220 package=THT]
  R6 = Resistor [tolerance=±5% resistance=220 package=THT]
  R7 = Resistor [tolerance=±5% resistance=220 package=THT]
  R8 = Resistor [tolerance=±5% resistance=220 package=THT]
  R9 = Resistor [tolerance=±5% resistance=220 package=THT]
  R10 = Resistor [tolerance=±5% resistance=220 package=THT]
  R11 = Resistor [tolerance=±5% resistance=220 package=THT]
  R12 = Resistor [tolerance=±5% resistance=220 package=THT]
  Q1 = NPN-Transistor [package="TO92 [THT]"]
  Q2 = PNP-Transistor [package="TO92 [THT]"]
  R13 = Resistor [tolerance=±5% resistance=220 package=THT]
  Q3 = NPN-Transistor [package="TO92 [THT]"]
  Q4 = NPN-Transistor [package="TO92 [THT]"]
  J1 = Screw terminal - 2 pins [package=THT]
  J2 = female pin header, 2 pins [form="♀ (female)"]
  J3 = female pin header, 2 pins [form="♀ (female)"]
  J4 = female pin header, 2 pins [form="♀ (female)"]
  J5 = female pin header, 2 pins [form="♀ (female)"]
  J6 = female pin header, 2 pins [form="♀ (female)"]
  J7 = female pin header, 2 pins [form="♀ (female)"]
  J8 = female pin header, 2 pins [form="♀ (female)"]
  J9 = female pin header, 2 pins [form="♀ (female)"]
  J10 = female pin header, 2 pins [form="♀ (female)"]
  J11 = female pin header, 2 pins [form="♀ (female)"]
  J12 = female pin header, 2 pins [form="♀ (female)"]
  J13 = female pin header, 2 pins [form="♀ (female)"]
  J14 = female pin header, 2 pins [form="♀ (female)"]
  J15 = female pin header, 2 pins [form="♀ (female)"]
  J16 = female pin header, 2 pins [form="♀ (female)"]
  J17 = female pin header, 2 pins [form="♀ (female)"]
  R14 = Resistor [tolerance=±5% resistance=220 package=THT]
  R15 = Resistor [tolerance=±5% resistance=220 package=THT]
  R16 = Resistor [tolerance=±5% resistance=220 package=THT]
  R17 = Resistor [tolerance=±5% resistance=220 package=THT]
  R18 = Resistor [tolerance=±5% resistance=220 package=THT]
  Q5 = NPN-Transistor [package="TO92 [THT]"]
  Q6 = NPN-Transistor [package="TO92 [THT]"]
  Q7 = NPN-Transistor [package="TO92 [THT]"]
  Q8 = NPN-Transistor [package="TO92 [THT]"]
  Q9 = NPN-Transistor [package="TO92 [THT]"]
  Q10 = NPN-Transistor [package="TO92 [THT]"]
  Q11 = NPN-Transistor [package="TO92 [THT]"]
  Q12 = NPN-Transistor [package="TO92 [THT]"]
  Q13 = NPN-Transistor [package="TO92 [THT]"]
  Q14 = NPN-Transistor [package="TO92 [THT]"]
  Q15 = NPN-Transistor [package="TO92 [THT]"]
  Q16 = NPN-Transistor [package="TO92 [THT]"]
  Q17 = NPN-Transistor [package="TO92 [THT]"]
  Q18 = NPN-Transistor [package="TO92 [THT]"]
  Q19 = NPN-Transistor [package="TO92 [THT]"]
  R19 = Resistor [tolerance=±5% resistance=220 package=THT]
  R20 = Resistor [tolerance=±5% resistance=220 package=THT]
  R21 = Resistor [tolerance=±5% resistance=220 package=THT]
  R22 = Resistor [tolerance=±5% resistance=220 package=THT]
  R23 = Resistor [tolerance=±5% resistance=220 package=THT]
  R24 = Resistor [tolerance=±5% resistance=220 package=THT]
  R25 = Resistor [tolerance=±5% resistance=220 package=THT]
  R26 = Resistor [tolerance=±5% resistance=220 package=THT]
  R27 = Resistor [tolerance=±5% resistance=220 package=THT]
  R28 = Resistor [tolerance=±5% resistance=220 package=THT]
  R29 = Resistor [tolerance=±5% resistance=220 package=THT]
  R30 = Resistor [tolerance=±5% resistance=220 package=THT]
  R31 = Resistor [tolerance=±5% resistance=220 package=THT]
  R32 = Resistor [tolerance=±5% resistance=220 package=THT]
  R33 = Resistor [tolerance=±5% resistance=220 package=THT]
  J18 = female pin header, 2 pins [form="♀ (female)"]
  Q20 = NPN-Transistor [package="TO92 [THT]"]
  Q21 = NPN-Transistor [package="TO92 [THT]"]
  Q22 = NPN-Transistor [package="TO92 [THT]"]
  Q23 = NPN-Transistor [package="TO92 [THT]"]
  Q24 = NPN-Transistor [package="TO92 [THT]"]
  Q25 = NPN-Transistor [package="TO92 [THT]"]
  Q26 = NPN-Transistor [package="TO92 [THT]"]
  Q27 = NPN-Transistor [package="TO92 [THT]"]
  Q28 = NPN-Transistor [package="TO92 [THT]"]
  Q29 = NPN-Transistor [package="TO92 [THT]"]
  Q30 = NPN-Transistor [package="TO92 [THT]"]
  Q31 = NPN-Transistor [package="TO92 [THT]"]
  Q32 = NPN-Transistor [package="TO92 [THT]"]
  J19 = female pin header, 5 pins [form="♀ (female)"]
  R34 = Resistor [tolerance=±5% resistance=220 package=THT]
  R35 = Resistor [tolerance=±5% resistance=220 package=THT]

nets:
  N1: U1.Pin_1, Q2.B
  N2: U1.Pin_4, J19.pin1
  N3: U1.Pin_5, U1.Pin_7, U1.Pin_8, U1.Pin_13, U1.Pin_22, Q1.E, Q1.B, Q1.C, Q2.C, R13.Pin_1, Q3.E, Q4.C, J1.pin1, J1.pin2, J2.pin1, J2.pin2, J3.pin1, J4.pin1, J5.pin1, J6.pin1, J7.pin1, J8.pin1, J9.pin1, J10.pin1, J11.pin1, J12.pin1, J13.pin1, J14.pin1, J15.pin1, J16.pin1, J17.pin1, R14.Pin_0, R14.Pin_1, Q5.E, Q6.C, Q7.E, Q8.E, Q9.E, Q10.E, Q11.E, Q12.E, Q13.E, Q14.E, Q15.E, Q16.E, Q17.E, Q18.E, Q19.E, J18.pin1, J18.pin2, Q20.C, Q21.C, Q22.C, Q23.C, Q24.C, Q25.C, Q26.C, Q27.C, Q28.B, Q28.C, Q29.C, Q30.C, Q31.C, Q32.C, R34.Pin_0, R35.Pin_0
  N4: U1.Pin_6, R34.Pin_1
  N5: U1.Pin_9, J19.pin2, R35.Pin_1
  N6: U1.Pin_10, J19.pin3
  N7: U1.Pin_11, J19.pin4
  N8: U1.Pin_12, J19.pin5
  N9: U1.Pin_14, Q20.B
  N10: U1.Pin_15, Q21.B
  N11: U1.Pin_16, Q22.B
  N12: U1.Pin_17, Q23.B
  N13: U1.Pin_18, Q24.B
  N14: U1.Pin_19, Q25.B
  N15: U1.Pin_20, Q26.B
  N16: U1.Pin_21, Q27.B
  N17: U1.Pin_23, Q29.B
  N18: U1.Pin_24, Q30.B
  N19: U1.Pin_25, Q31.B
  N20: U1.Pin_26, Q32.B
  N21: U1.Pin_27, Q6.B
  N22: U1.Pin_28, Q4.B
  N23: R2.Pin_0, Q4.E
  N24: R2.Pin_1, Q3.B
  N25: R3.Pin_0, Q6.E
  N26: R3.Pin_1, Q5.B
  N27: R4.Pin_0, Q32.E
  N28: R4.Pin_1, Q16.B
  N29: R5.Pin_0, Q31.E
  N30: R5.Pin_1, Q15.B
  N31: R6.Pin_0, Q30.E
  N32: R6.Pin_1, Q14.B
  N33: R7.Pin_0, Q29.E
  N34: R7.Pin_1, Q13.B
  N35: R8.Pin_0, Q28.E
  N36: R8.Pin_1, Q12.B
  N37: R9.Pin_0, Q27.E
  N38: R9.Pin_1, Q11.B
  N39: R10.Pin_0, Q26.E
  N40: R10.Pin_1, Q10.B
  N41: R11.Pin_0, Q25.E
  N42: R11.Pin_1, Q9.B
  N43: R12.Pin_0, Q24.E
  N44: R12.Pin_1, Q8.B
  N45: Q2.E, R13.Pin_0
  N46: Q3.C, R19.Pin_0
  N47: J3.pin2, R19.Pin_1
  N48: J4.pin2, R20.Pin_1
  N49: J5.pin2, R21.Pin_1
  N50: J6.pin2, R22.Pin_1
  N51: J7.pin2, R23.Pin_1
  N52: J8.pin2, R24.Pin_1
  N53: J9.pin2, R25.Pin_1
  N54: J10.pin2, R26.Pin_1
  N55: J11.pin2, R27.Pin_1
  N56: J12.pin2, R28.Pin_1
  N57: J13.pin2, R29.Pin_1
  N58: J14.pin2, R30.Pin_1
  N59: J15.pin2, R31.Pin_1
  N60: J16.pin2, R32.Pin_1
  N61: J17.pin2, R33.Pin_1
  N62: R15.Pin_0, Q23.E
  N63: R15.Pin_1, Q7.B
  N64: R16.Pin_0, Q22.E
  N65: R16.Pin_1, Q19.B
  N66: R17.Pin_0, Q21.E
  N67: R17.Pin_1, Q18.B
  N68: R18.Pin_0, Q20.E
  N69: R18.Pin_1, Q17.B
  N70: Q5.C, R20.Pin_0
  N71: Q7.C, R30.Pin_0
  N72: Q8.C, R29.Pin_0
  N73: Q9.C, R28.Pin_0
  N74: Q10.C, R27.Pin_0
  N75: Q11.C, R26.Pin_0
  N76: Q12.C, R25.Pin_0
  N77: Q13.C, R24.Pin_0
  N78: Q14.C, R23.Pin_0
  N79: Q15.C, R22.Pin_0
  N80: Q16.C, R21.Pin_0
  N81: Q17.C, R33.Pin_0
  N82: Q18.C, R32.Pin_0
  N83: Q19.C, R31.Pin_0
