# Fritzing sketch Light Module - ULN2803A - 8ch - SM (saved by Fritzing 0.6.4b)
breadboards: 1

parts:
  U1 = 74HC595 [package="DIP16 [THT]"]
  IC1 = ULN2803A [package=THT]
  L7 = female pin header, 2 pins [form="♀ (female)"]
  L6 = female pin header, 2 pins [form="♀ (female)"]
  L0 = female pin header, 2 pins [form="♀ (female)"]
  L5 = female pin header, 2 pins [form="♀ (female)"]
  L4 = female pin header, 2 pins [form="♀ (female)"]
  L3 = female pin header, 2 pins [form="♀ (female)"]
  L2 = female pin header, 2 pins [form="♀ (female)"]
  L1 = female pin header, 2 pins [form="♀ (female)"]
  R1 = Resistor [tolerance=±5% resistance=220 package=THT]
  R2 = Resistor [tolerance=±5% resistance=220 package=THT]
  R3 = Resistor [tolerance=±5% resistance=220 package=THT]
  R4 = Resistor [tolerance=±5% resistance=220 package=THT]
  R5 = Resistor [tolerance=±5% resistance=220 package=THT]
  R6 = Resistor [tolerance=±5% resistance=220 package=THT]
  R7 = Resistor [tolerance=±5% resistance=220 package=THT]
  R8 = Resistor [tolerance=±5% resistance=220 package=THT]
  Light_Power_In = Screw terminal - 2 pins [package=THT]
  Data_In = female pin header, 5 pins [form="♀ (female)"]
  Data_Out = female pin header, 5 pins [form="♀ (female)"]
  R10 = Resistor [tolerance=±5% resistance=100 package="0805 [SMD]"]
  DC_On = smd LED [color="Red (633nm)" package="0805 [SMD]"]
  DC_Power1 = female pin header, 2 pins [form="♀ (female)"]
  R11 = Resistor [tolerance=±5% resistance=220 package="0805 [SMD]"]
  LED1 = smd LED [color="Red (633nm)" package="0805 [SMD]"]
  R9 = Resistor [tolerance=±5% resistance=220 package=THT]

nets:
  N1: U1.Q1, IC1.In_7
  N2: U1.Q2, IC1.In_6
  N3: U1.Q3, IC1.In_5
  N4: U1.Q4, IC1.In_4
  N5: U1.Q5, IC1.In_3
  N6: U1.Q6, IC1.In_2
  N7: U1.Q7, IC1.In_1
  N8: U1.GND, U1.OE, IC1.0V, Light_Power_In.pin2, R9.Pin_0
  N9: U1.Q7', Data_Out.pin1
  N10: U1.SH_CP, Data_In.pin2, Data_Out.pin3
  N11: U1.ST_CP, Data_In.pin3, Data_Out.pin4
  N12: U1.DS, Data_In.pin5
  N13: U1.Q0, IC1.In_8
  N14: U1.VCC, DC_On.cathode, DC_Power1.pin1
  N15: IC1.COM_-_Common, L7.pin2, L6.pin2, L0.pin2, L5.pin2, L4.pin2, L3.pin2, L2.pin2, L1.pin2, Light_Power_In.pin1, LED1.anode
  N16: IC1.Out_8, R8.Pin_0
  N17: IC1.Out_7, R7.Pin_0
  N18: IC1.Out_6, R6.Pin_0
  N19: IC1.Out_5, R5.Pin_0
  N20: IC1.Out_4, R4.Pin_0
  N21: IC1.Out_3, R3.Pin_0
  N22: IC1.Out_2, R2.Pin_0
  N23: IC1.Out_1, R1.Pin_0
  N24: L7.pin1, R1.Pin_1
  N25: L6.pin1, R2.Pin_1
  N26: L0.pin1, R8.Pin_1
  N27: L5.pin1, R3.Pin_1
  N28: L4.pin1, R4.Pin_1
  N29: L3.pin1, R5.Pin_1
  N30: L2.pin1, R6.Pin_1
  N31: L1.pin1, R7.Pin_1
  N32: R10.Pin_0, DC_Power1.pin2, R11.Pin_0
  N33: R10.Pin_1, DC_On.anode
  N34: R11.Pin_1, LED1.cathode
