# Fritzing sketch MSGEQ7 Graphic Equalizer Board (saved by Fritzing 0.7.0b)
breadboards: 1

parts:
  IC1 = IC, DIP package, 8 pins [chip_label=IC spacing=300mil]
  J1 = female pin header, 2 pins [form="♀ (female)"]
  C1 = Ceramic Capacitor [capacitance=33pF package="100 mil [THT, multilayer]"]
  J2 = female pin header, 3 pins [form="♀ (female)"]
  J3 = female pin header, 3 pins [form="♀ (female)"]
  C2 = Ceramic Capacitor [capacitance=100nF package="100 mil [THT, multilayer]"]
  C3 = Ceramic Capacitor [capacitance=10nF package="100 mil [THT, multilayer]"]
  C4 = Ceramic Capacitor [capacitance=100nF package="100 mil [THT, multilayer]"]
  R1 = Resistor [tolerance=±5% resistance=200k package=THT]

nets:
  N1: IC1.pin1, J1.pin2, C4.0, R1.Pin_0
  N2: IC1.pin2, J1.pin1, C1.0, J3.pin2, C2.0, C4.1
  N3: IC1.pin3, J2.pin1
  N4: IC1.pin4, J2.pin2
  N5: IC1.pin5, C3.1
  N6: IC1.pin6, C2.1
  N7: IC1.pin7, J2.pin3
  N8: IC1.pin8, C1.1, R1.Pin_1
  N9: J3.pin1, J3.pin3, C3.0
