# Fritzing sketch POV Sheild - v1 (saved by Fritzing 0.6.4b)
breadboards: 1

parts:
  LED1 = LED - 5mm [color="Red (633nm)" package="5 mm [THT]"]
  LED2 = LED - 5mm [color="Red (633nm)" package="5 mm [THT]"]
  LED3 = LED - 5mm [color="Red (633nm)" package="5 mm [THT]"]
  LED4 = LED - 5mm [color="Red (633nm)" package="5 mm [THT]"]
  LED5 = LED - 5mm [color="Red (633nm)" package="5 mm [THT]"]
  LED6 = LED - 5mm [color="Red (633nm)" package="5 mm [THT]"]
  LED7 = LED - 5mm [color="Red (633nm)" package="5 mm [THT]"]
  LED8 = LED - 5mm [color="Red (633nm)" package="5 mm [THT]"]
  R1 = Resistor [tolerance=±5% resistance=220 package=THT]
  R2 = Resistor [tolerance=±5% resistance=220 package=THT]
  R3 = Resistor [tolerance=±5% resistance=220 package=THT]
  R4 = Resistor [tolerance=±5% resistance=220 package=THT]
  U1 = 74HC595 [package="DIP16 [THT]"]
  J1 = female pin header, 5 pins [form="♀ (female)"]
  R5 = Resistor [tolerance=±5% resistance=220 package=THT]
  R6 = Resistor [tolerance=±5% resistance=220 package=THT]
  R7 = Resistor [tolerance=±5% resistance=220 package=THT]
  R8 = Resistor [tolerance=±5% resistance=220 package=THT]

nets:
  N1: LED1.cathode, R1.Pin_0
  N2: LED1.anode, U1.Q7
  N3: LED2.cathode, R2.Pin_0
  N4: LED2.anode, U1.Q6
  N5: LED3.cathode, R3.Pin_0
  N6: LED3.anode, U1.Q5
  N7: LED4.cathode, R4.Pin_0
  N8: LED4.anode, U1.Q4
  N9: LED5.cathode, R5.Pin_0
  N10: LED5.anode, U1.Q3
  N11: LED6.cathode, R6.Pin_0
  N12: LED6.anode, U1.Q2
  N13: LED7.cathode, R7.Pin_0
  N14: LED7.anode, U1.Q1
  N15: LED8.cathode, R8.Pin_0
  N16: LED8.anode, U1.Q0
  N17: R1.Pin_1, R2.Pin_1, R3.Pin_1, R4.Pin_1, U1.GND, U1.OE, J1.pin1, R5.Pin_1, R6.Pin_1, R7.Pin_1, R8.Pin_1
  N18: U1.MR, U1.VCC, J1.pin2
  N19: U1.SH_CP, J1.pin5
  N20: U1.ST_CP, J1.pin4
  N21: U1.DS, J1.pin3
