# Fritzing sketch POV Sheild - v2 (saved by Fritzing 0.6.4b)
breadboards: 1

parts:
  U1 = 74HC595 [package="DIP16 [THT]"]
  J1 = female pin header, 5 pins [form="♀ (female)"]
  LED1 = smd LED [color="Red (633nm)" package="0805 [SMD]"]
  R1 = Resistor [tolerance=±5% resistance=220 package="0805 [SMD]"]
  LED2 = smd LED [color="Red (633nm)" package="0805 [SMD]"]
  LED3 = smd LED [color="Red (633nm)" package="0805 [SMD]"]
  R2 = Resistor [tolerance=±5% resistance=220 package="0805 [SMD]"]
  R3 = Resistor [tolerance=±5% resistance=220 package="0805 [SMD]"]
  LED4 = smd LED [color="Red (633nm)" package="0805 [SMD]"]
  LED5 = smd LED [color="Red (633nm)" package="0805 [SMD]"]
  LED6 = smd LED [color="Red (633nm)" package="0805 [SMD]"]
  LED7 = smd LED [color="Red (633nm)" package="0805 [SMD]"]
  LED8 = smd LED [color="Red (633nm)" package="0805 [SMD]"]
  R4 = Resistor [tolerance=±5% resistance=220 package="0805 [SMD]"]
  R5 = Resistor [tolerance=±5% resistance=220 package="0805 [SMD]"]
  R6 = Resistor [tolerance=±5% resistance=220 package="0805 [SMD]"]
  R7 = Resistor [tolerance=±5% resistance=220 package="0805 [SMD]"]
  R8 = Resistor [tolerance=±5% resistance=220 package="0805 [SMD]"]

nets:
  N1: U1.Q1, LED7.anode
  N2: U1.Q2, LED6.anode
  N3: U1.Q3, LED5.anode
  N4: U1.Q4, LED4.anode
  N5: U1.Q5, LED3.anode
  N6: U1.Q6, LED2.anode
  N7: U1.Q7, LED1.anode
  N8: U1.GND, U1.OE, J1.pin1, R1.Pin_1, R2.Pin_1, R3.Pin_1, R4.Pin_1, R5.Pin_1, R6.Pin_1, R7.Pin_1, R8.Pin_1
  N9: U1.MR, U1.VCC, J1.pin2
  N10: U1.SH_CP, J1.pin5
  N11: U1.ST_CP, J1.pin4
  N12: U1.DS, J1.pin3
  N13: U1.Q0, LED8.anode
  N14: LED1.cathode, R1.Pin_0
  N15: LED2.cathode, R2.Pin_0
  N16: LED3.cathode, R3.Pin_0
  N17: LED4.cathode, R4.Pin_0
  N18: LED5.cathode, R5.Pin_0
  N19: LED6.cathode, R6.Pin_0
  N20: LED7.cathode, R7.Pin_0
  N21: LED8.cathode, R8.Pin_0
