# Fritzing sketch PWM Light Module (saved by Fritzing 0.7.0b)
breadboards: 1

parts:
  IC1 = IC, DIP package, 28 pins [chip_label=IC spacing=300mil]
  U2 = IC, DIP package, 20 pins [chip_label=IC spacing=300mil]
  U1 = IC, DIP package, 20 pins [chip_label=IC spacing=300mil]
  IC2 = ULN2803A [package=THT]
  IC3 = ULN2803A [package=THT]

nets:
  N1: IC1.pin1, U2.pin3
  N2: IC1.pin2, U2.pin4
  N3: IC1.pin3, U2.pin5
  N4: IC1.pin4, U2.pin6
  N5: IC1.pin5, U2.pin7
  N6: IC1.pin6, U2.pin8
  N7: IC1.pin7, U2.pin9
  N8: IC1.pin8, U1.pin2
  N9: IC1.pin9, U1.pin3
  N10: IC1.pin10, U1.pin4
  N11: IC1.pin11, U1.pin5
  N12: IC1.pin12, U1.pin6
  N13: IC1.pin13, U1.pin7
  N14: IC1.pin14, U1.pin8
  N15: IC1.pin15, U1.pin9
  N16: IC1.pin28, U2.pin2
  GND: U2.pin10, U1.pin10, IC2.0V, IC3.0V
  N17: U2.pin11, IC2.In_8
  N18: U2.pin12, IC2.In_7
  N19: U2.pin13, IC2.In_6
  N20: U2.pin14, IC2.In_5
  N21: U2.pin15, IC2.In_4
  N22: U2.pin16, IC2.In_3
  N23: U2.pin17, IC2.In_2
  N24: U2.pin18, IC2.In_1
  5V: U2.pin20, U1.pin20
  N25: U1.pin11, IC3.In_8
  N26: U1.pin12, IC3.In_7
  N27: U1.pin13, IC3.In_6
  N28: U1.pin14, IC3.In_5
  N29: U1.pin15, IC3.In_4
  N30: U1.pin16, IC3.In_3
  N31: U1.pin17, IC3.In_2
  N32: U1.pin18, IC3.In_1
  12V: IC2.COM_-_Common, IC3.COM_-_Common
