# Fritzing sketch RGB Module (saved by Fritzing 0.6.3b)
breadboards: 1

parts:
  LED1 = RGB LED (com. cathode, rbg) [package="5 mm [THT]"]
  LED2 = RGB LED (com. cathode, rbg) [package="5 mm [THT]"]
  LED3 = RGB LED (com. cathode, rbg) [package="5 mm [THT]"]
  J1 = female pin header, 4 pins [form="♀ (female)"]
  R1 = Resistor [tolerance=±5% resistance=220 package=THT]
  R2 = Resistor [tolerance=±5% resistance=220 package=THT]
  R3 = Resistor [tolerance=±5% resistance=220 package=THT]
  R4 = Resistor [tolerance=±5% resistance=220 package=THT]
  R5 = Resistor [tolerance=±5% resistance=220 package=THT]
  R4_2 = Resistor [tolerance=±5% resistance=220 package=THT]
  R7 = Resistor [tolerance=±5% resistance=220 package=THT]
  R8 = Resistor [tolerance=±5% resistance=220 package=THT]
  R9 = Resistor [tolerance=±5% resistance=220 package=THT]

nets:
  N1: LED1.red_anode, R9.Pin_0
  N2: LED1.common_cathode, LED2.common_cathode, LED3.common_cathode, J1.pin1
  N3: LED1.blue_anode, R7.Pin_0
  N4: LED1.green_anode, R8.Pin_0
  N5: LED2.red_anode, R4_2.Pin_0
  N6: LED2.blue_anode, R4.Pin_0
  N7: LED2.green_anode, R5.Pin_0
  N8: LED3.red_anode, R3.Pin_0
  N9: LED3.blue_anode, R2.Pin_0
  N10: LED3.green_anode, R1.Pin_0
  N11: J1.pin2, R3.Pin_1, R4_2.Pin_1, R9.Pin_1
  N12: J1.pin3, R2.Pin_1, R4.Pin_1, R7.Pin_1
  N13: J1.pin4, R1.Pin_1, R5.Pin_1, R8.Pin_1
