# Fritzing sketch RGB NPN Driver (saved by Fritzing 0.7.1b)
breadboards: 1

parts:
  Q1 = NPN-Transistor [package="TO92 [THT]"]
  Q2 = NPN-Transistor [package="TO92 [THT]"]
  R1 = Resistor [tolerance=±5% resistance=220 package=THT]
  J1 = female pin header, 5 pins [form="♀ (female)"]
  Q5 = NPN-Transistor [package="TO92 [THT]"]
  Q6 = NPN-Transistor [package="TO92 [THT]"]
  R2 = Resistor [tolerance=±5% resistance=220 package=THT]
  Q7 = NPN-Transistor [package="TO92 [THT]"]
  Q8 = NPN-Transistor [package="TO92 [THT]"]
  R3 = Resistor [tolerance=±5% resistance=220 package=THT]
  J2 = female pin header, 4 pins [form="♀ (female)"]

nets:
  N1: Q1.E, Q2.E, J1.pin2, Q5.E, Q6.E, Q7.E, Q8.E
  N2: Q1.B, Q2.B, R1.Pin_1
  N3: Q1.C, Q2.C, J2.pin3
  N4: R1.Pin_0, J1.pin3
  N5: J1.pin1, J2.pin4
  N6: J1.pin4, R2.Pin_0
  N7: J1.pin5, R3.Pin_0
  N8: Q5.B, Q6.B, R2.Pin_1
  N9: Q5.C, Q6.C, J2.pin2
  N10: Q7.B, Q8.B, R3.Pin_1
  N11: Q7.C, Q8.C, J2.pin1
