# Fritzing sketch RGB Shift - v1 (saved by Fritzing 0.7.0b)
breadboards: 1

parts:
  Shift1 = 74HC595 [package="DIP16 [THT]"]
  LED1 = RGB LED (com. cathode, rbg) [package="5 mm [THT]"]
  LED2 = RGB LED (com. cathode, rbg) [package="5 mm [THT]"]
  J1 = female pin header, 5 pins [form="♀ (female)"]
  R1 = Resistor [tolerance=±5% resistance=100 package=THT]
  R2 = Resistor [tolerance=±5% resistance=150 package=THT]
  R3 = Resistor [tolerance=±5% resistance=150 package=THT]
  R4 = Resistor [tolerance=±5% resistance=100 package=THT]
  R5 = Resistor [tolerance=±5% resistance=150 package=THT]
  R6 = Resistor [tolerance=±5% resistance=150 package=THT]
  Shift2 = 74HC595 [package="DIP16 [THT]"]
  R7 = Resistor [tolerance=±5% resistance=100 package=THT]
  R8 = Resistor [tolerance=±5% resistance=150 package=THT]
  R9 = Resistor [tolerance=±5% resistance=150 package=THT]
  LED3 = RGB LED (com. cathode, rbg) [package="5 mm [THT]"]
  LED4 = RGB LED (com. cathode, rbg) [package="5 mm [THT]"]
  LED5 = RGB LED (com. cathode, rbg) [package="5 mm [THT]"]
  R10 = Resistor [tolerance=±5% resistance=100 package=THT]
  R11 = Resistor [tolerance=±5% resistance=150 package=THT]
  R12 = Resistor [tolerance=±5% resistance=150 package=THT]
  R13 = Resistor [tolerance=±5% resistance=100 package=THT]
  R14 = Resistor [tolerance=±5% resistance=150 package=THT]
  R15 = Resistor [tolerance=±5% resistance=150 package=THT]

nets:
  N1: Shift1.Q1, R2.Pin_1
  N2: Shift1.Q2, R3.Pin_1
  N3: Shift1.Q3, R4.Pin_1
  N4: Shift1.Q4, R5.Pin_1
  N5: Shift1.Q5, R6.Pin_1
  N6: Shift1.Q6, R7.Pin_1
  N7: Shift1.Q7, R8.Pin_1
  GND: Shift1.GND, Shift1.OE, LED1.common_cathode, LED2.common_cathode, J1.pin2, Shift2.GND, Shift2.OE, LED3.blue_anode, LED4.common_cathode, LED5.common_cathode
  N8: Shift1.Q7', Shift2.DS
  VCC: Shift1.MR, Shift1.VCC, J1.pin1, Shift2.MR, Shift2.VCC
  N9: Shift1.SH_CP, J1.pin5, Shift2.SH_CP
  N10: Shift1.ST_CP, J1.pin4, Shift2.ST_CP
  N11: Shift1.DS, J1.pin3
  N12: Shift1.Q0, R1.Pin_1
  N13: LED1.red_anode, R1.Pin_0
  N14: LED1.blue_anode, R2.Pin_0
  N15: LED1.green_anode, R3.Pin_0
  N16: LED2.red_anode, R4.Pin_0
  N17: LED2.blue_anode, R5.Pin_0
  N18: LED2.green_anode, R6.Pin_0
  N19: Shift2.Q1, R10.Pin_1
  N20: Shift2.Q2, R11.Pin_1
  N21: Shift2.Q3, R12.Pin_1
  N22: Shift2.Q4, R13.Pin_1
  N23: Shift2.Q5, R14.Pin_1
  N24: Shift2.Q6, R15.Pin_1
  N25: Shift2.Q0, R9.Pin_1
  N26: R7.Pin_0, LED3.red_anode
  N27: R8.Pin_0, LED3.common_cathode
  N28: R9.Pin_0, LED3.green_anode
  N29: LED4.red_anode, R10.Pin_0
  N30: LED4.blue_anode, R11.Pin_0
  N31: LED4.green_anode, R12.Pin_0
  N32: LED5.red_anode, R13.Pin_0
  N33: LED5.blue_anode, R14.Pin_0
  N34: LED5.green_anode, R15.Pin_0
