# Fritzing sketch RGB Strip Controller (saved by Fritzing 0.7.1b)
breadboards: 1

parts:
  Q1 = Basic FET N-Channel [package="DPak [SMD]"]
  Q2 = Basic FET N-Channel [package="DPak [SMD]"]
  Q3 = Basic FET N-Channel [package="DPak [SMD]"]
  J1 = female pin header, 4 pins [form="♀ (female)"]
  J2 = female pin header, 5 pins [form="♀ (female)"]

nets:
  N1: Q1.Gate, J2.pin5
  N2: Q1.drain, J1.pin4
  N3: Q1.source, Q2.source, Q3.source, J2.pin2
  N4: Q2.Gate, J2.pin3
  N5: Q2.drain, J1.pin2
  N6: Q3.Gate, J2.pin4
  N7: Q3.drain, J1.pin3
  N8: J1.pin1, J2.pin1
