# Fritzing sketch RGB Switching Module - SS (saved by Fritzing 0.7.0b)
breadboards: 1

parts:
  Q10 = Basic FET N-Channel [package="DPak [SMD]"]
  Q14 = Basic FET N-Channel [package="DPak [SMD]"]
  R1 = Resistor [tolerance=±5% resistance=220 package=THT]
  R2 = Resistor [tolerance=±5% resistance=220 package=THT]
  R3 = Resistor [tolerance=±5% resistance=220 package=THT]
  J2 = female pin header, 4 pins [form="♀ (female)"]
  Q15 = Basic FET N-Channel [package="DPak [SMD]"]
  J1 = female pin header, 3 pins [form="♀ (female)"]
  J3 = Screw terminal - 2 pins [package=THT]

nets:
  N1: Q10.Gate, R3.Pin_0
  N2: Q10.drain, J2.pin3
  N3: Q10.source, Q14.source, Q15.source, J3.pin1
  N4: Q14.Gate, R2.Pin_0
  N5: Q14.drain, J2.pin2
  N6: R1.Pin_0, Q15.Gate
  N7: R1.Pin_1, J1.pin3
  N8: R2.Pin_1, J1.pin1
  N9: R3.Pin_1, J1.pin2
  N10: J2.pin1, J3.pin2
  N11: J2.pin4, Q15.drain
