# Fritzing sketch SMD Arduino (saved by Fritzing 0.7.1b)
breadboards: 1

parts:
  J1 = female pin header, 2 pins [form="♀ (female)"]
  U1 = Voltage Regulator - 5V [package="DPak [SMD]"]
  C1 = Electrolytic Capacitor [capacitance=1µF package="0405 [SMD, electrolytic]"]
  C2 = Electrolytic Capacitor [capacitance=1µF package="0405 [SMD, electrolytic]"]
  U2 = atmega168 [package=dip]
  XTAL1 = Crystal [frequency="16 Mhz" package=SMD]
  J2 = female pin header, 6 pins [form="♀ (female)"]
  J3 = female pin header, 5 pins [form="♀ (female)"]
  J4 = female pin header, 5 pins [form="♀ (female)"]
  J5 = female pin header, 4 pins [form="♀ (female)"]
  J6 = female pin header, 4 pins [form="♀ (female)"]
  J7 = female pin header, 2 pins [form="♀ (female)"]
  C3 = Tantalum Capacitor [capacitance="1 μF" package="B 3528 [SMD, tantalum]"]
  C4 = Tantalum Capacitor [capacitance="1 μF" package="B 3528 [SMD, tantalum]"]
  R1 = Resistor [tolerance=±5% resistance=220 package="0805 [SMD]"]
  J8 = female pin header, 1 pin [form="♀ (female)"]
  S1 = Pushbutton [package=THT]
  LED1 = smd LED [color="Red (633nm)" package="0805 [SMD]"]
  R2 = Resistor [tolerance=±5% resistance=220 package="0805 [SMD]"]
  LED2 = smd LED [color="Red (633nm)" package="0805 [SMD]"]
  R3 = Resistor [tolerance=±5% resistance=220 package="0805 [SMD]"]
  J9 = female pin header, 3 pins [form="♀ (female)"]
  J10 = female pin header, 3 pins [form="♀ (female)"]
  C5 = Ceramic Capacitor [capacitance=100nF package="0805 [SMD, multilayer]"]

nets:
  N1: J1.pin1, U1.input_voltage, C1.+
  GND: J1.pin2, U1.GND, C2.-, U2.GND, J6.pin4, J7.pin1, S1.leg0, R2.Pin_0, LED2.anode, J10.pin1
  N2: U1.output_voltage, C2.+, U2.VCC, J6.pin3, J7.pin2, R1.Pin_0, LED1.cathode, J10.pin3
  N3: U2.RESET, R1.Pin_1, S1.leg1, C5.1
  N4: U2.D0_(RX), J4.pin1, J6.pin1
  N5: U2.D1_(TX), J4.pin2, J6.pin2
  N6: U2.D2, J4.pin3
  N7: U2.D3_(PWM), J4.pin4
  N8: U2.D4, J4.pin5
  N9: U2.XLAT1, XTAL1.pin_0, C3.-
  N10: U2.XLAT2, XTAL1.pin_1, C4.-
  N11: U2.D5_(PWM), J5.pin1
  N12: U2.D6_(PWM), J5.pin2
  N13: U2.D7, J5.pin3
  N14: U2.D8, J5.pin4
  N15: U2.D9_(PWM), J3.pin5
  N16: U2.D10_(PWM), J3.pin4
  N17: U2.D11_(PWM), J3.pin3, J9.pin3
  N18: U2.D12, J3.pin2, J9.pin2
  N19: U2.D13, J3.pin1, R3.Pin_0, J9.pin1
  N20: U2.AVCC, U2.AREF
  N21: U2.A0, J2.pin6
  N22: U2.A1, J2.pin5
  N23: U2.A2, J2.pin4
  N24: U2.A3, J2.pin3
  N25: U2.A4, J2.pin2
  N26: U2.A5, J2.pin1
  N27: C3.+, C4.+
  N28: J8.pin1, J10.pin2, C5.0
  N29: LED1.anode, R2.Pin_1
  N30: LED2.cathode, R3.Pin_1
