# Fritzing sketch SMD LED Sheild (saved by Fritzing 0.6.4b)
breadboards: 1

parts:
  J1 = female pin header, 5 pins [form="♀ (female)"]
  R1 = Resistor [tolerance=±5% resistance=220 package="0805 [SMD]"]
  R2 = Resistor [tolerance=±5% resistance=220 package="0805 [SMD]"]
  LED2 = smd LED [color="Red (633nm)" package="0805 [SMD]"]
  LED1 = smd LED [color="Red (633nm)" package="0805 [SMD]"]

nets:
  N1: J1.pin1, R1.Pin_0
  N2: J1.pin4, LED2.anode
  N3: J1.pin5, LED1.anode
  N4: R1.Pin_1, LED1.cathode
  N5: R2.Pin_1, LED2.cathode
