# Fritzing sketch SerLCD (saved by Fritzing 0.7.1b)
breadboards: 1

parts:
  LCD1 = LCD screen
  U1 = 74HC595 [package="DIP16 [THT]"]
  J2 = female pin header, 2 pins [form="♀ (female)"]
  J1 = female pin header, 3 pins [form="♀ (female)"]

nets:
  VSS: LCD1.VSS, LCD1.R/W, U1.GND, U1.OE, J2.pin1
  VDD: LCD1.VDD, U1.MR, U1.VCC, J2.pin2
  N1: LCD1.RS, U1.Q2
  N2: LCD1.E, U1.ST_CP, J1.pin1
  N3: LCD1.DB4, U1.Q3
  N4: LCD1.DB5, U1.Q4
  N5: LCD1.DB6, U1.Q5
  N6: LCD1.DB7, U1.Q6
  N7: U1.SH_CP, J1.pin3
  N8: U1.DS, J1.pin2
