# Fritzing sketch Simple Motor Control (saved by Fritzing 0.7.0b)
breadboards: 1

parts:
  Q2 = NPN-Transistor [package="TO92 [THT]"]
  R1 = Resistor [tolerance=±5% resistance=220 package=THT]
  R2 = Resistor [tolerance=±5% resistance=220 package=THT]
  J1 = female pin header, 3 pins [form="♀ (female)"]
  J2 = Screw terminal - 2 pins [package=THT]
  J3 = female pin header, 2 pins [form="♀ (female)"]
  J4 = female pin header, 2 pins [form="♀ (female)"]
  Q1 = NPN-Transistor [package="TO92 [THT]"]

nets:
  N1: Q2.E, J1.pin1, J2.pin2, Q1.E
  N2: Q2.B, R1.Pin_0
  N3: Q2.C, J3.pin2
  N4: R1.Pin_1, J1.pin2
  N5: R2.Pin_0, Q1.B
  N6: R2.Pin_1, J1.pin3
  N7: J2.pin1, J3.pin1, J4.pin1
  N8: J4.pin2, Q1.C
