# Fritzing sketch Single RGB (saved by Fritzing 0.6.4b)
breadboards: 1

parts:
  LED1 = RGB LED (com. cathode, rbg) [package="5 mm [THT]"]
  R1 = Resistor [tolerance=±5% resistance=220 package=THT]
  R2 = Resistor [tolerance=±5% resistance=220 package=THT]
  R3 = Resistor [tolerance=±5% resistance=220 package=THT]
  J1 = female pin header, 4 pins [form="♀ (female)"]

nets:
  N1: LED1.red_anode, R3.Pin_0
  N2: LED1.common_cathode, J1.pin3
  N3: LED1.blue_anode, R2.Pin_0
  N4: LED1.green_anode, R1.Pin_0
  N5: R1.Pin_1, J1.pin1
  N6: R2.Pin_1, J1.pin2
  N7: R3.Pin_1, J1.pin4

notes:
  RGB Tester (Stephen Delaney)
