# Fritzing sketch TQFP32 Adaptor (saved by Fritzing 0.7.1b)
breadboards: 1

parts:
  IC1 = TQFP32-5MM [chip_label=IC spacing=300mil package=TQFP]
  J1 = female pin header, 16 pins [form="♀ (female)"]
  J2 = female pin header, 16 pins [form="♀ (female)"]

nets:
  N1: IC1.1, J2.pin1
  N2: IC1.2, J2.pin2
  N3: IC1.3, J2.pin3
  N4: IC1.4, J2.pin4
  N5: IC1.5, J2.pin5
  N6: IC1.6, J2.pin6
  N7: IC1.7, J2.pin7
  N8: IC1.8, J2.pin8
  N9: IC1.9, J2.pin9
  N10: IC1.10, J2.pin10
  N11: IC1.11, J2.pin11
  N12: IC1.12, J2.pin12
  N13: IC1.13, J2.pin13
  N14: IC1.14, J2.pin14
  N15: IC1.15, J2.pin15
  N16: IC1.16, J2.pin16
  N17: IC1.17, J1.pin16
  N18: IC1.18, J1.pin15
  N19: IC1.19, J1.pin14
  N20: IC1.20, J1.pin13
  N21: IC1.21, J1.pin12
  N22: IC1.22, J1.pin11
  N23: IC1.23, J1.pin10
  N24: IC1.24, J1.pin9
  N25: IC1.25, J1.pin8
  N26: IC1.26, J1.pin7
  N27: IC1.27, J1.pin6
  N28: IC1.28, J1.pin5
  N29: IC1.29, J1.pin4
  N30: IC1.30, J1.pin3
  N31: IC1.31, J1.pin2
  N32: IC1.32, J1.pin1
