# Fritzing sketch l297-298 - Stepper Controller (saved by Fritzing 0.7.1b)
breadboards: 1

parts:
  L298N1 = L298N
  J1 = female pin header, 4 pins [form="♀ (female)"]
  J2 = female pin header, 5 pins [form="♀ (female)"]
  IC1 = IC, DIP package, 20 pins [chip_label=IC spacing=300mil]
  J3 = Screw terminal - 2 pins [package=THT]
  R1 = Resistor [tolerance=±5% resistance=220 package=THT]
  R2 = Resistor [tolerance=±5% resistance=220 package=THT]
  C1 = Electrolytic Capacitor [capacitance=1µF package="100 mil [THT, electrolytic]"]

nets:
  N1: L298N1.C1, IC1.pin14, R1.Pin_1
  N2: L298N1.C2, J1.pin1
  N3: L298N1.C3, J1.pin2
  N4: L298N1.C4, IC1.pin13, J3.pin2, R1.Pin_0, R2.Pin_1, C1.+
  N5: L298N1.C5, IC1.pin4
  N6: L298N1.C6, IC1.pin5
  N7: L298N1.C7, IC1.pin6
  N8: L298N1.C8, J3.pin1, C1.-
  N9: L298N1.C9, J2.pin2, IC1.pin12
  N10: L298N1.C10, IC1.pin7
  N11: L298N1.C11, IC1.pin8
  N12: L298N1.C12, IC1.pin9
  N13: L298N1.C13, J1.pin3
  N14: L298N1.C14, J1.pin4
  N15: L298N1.C15, R2.Pin_0
  N16: J2.pin1, IC1.pin10
  N17: J2.pin3, IC1.pin17
  N18: J2.pin4, IC1.pin18
  N19: J2.pin5, IC1.pin2
